// Digital circuit 1bit_8xAND.dig as structural Verilog
module _1bit_8xAND (
  input  _1,
  input  _2,
  input  _3,
  input  _4,
  input  _5,
  input  _6,
  input  _7,
  input  _8,
  output o
);

  wire and_1_out, and_2_out;

  and and_1 (and_1_out, _1, _2, _3, _4, _5);
  and and_2 (and_2_out, _6, _7, _8);
  and and_3 (o, and_1_out, and_2_out);
endmodule
