// Digital circuit 1bit_Adder.dig as structural Verilog
module _1bit_Adder (
  input  a,
  input  b,
  input  c_in,
  output s,
  output c_out
);

  wire and_1_out, and_2_out, xor_1_out;

  xor xor_1 (xor_1_out, a, b);
  and and_1 (and_1_out, a, b);
  or or_1 (c_out, and_2_out, and_1_out);
  xor xor_2 (s, c_in, xor_1_out);
  and and_2 (and_2_out, c_in, xor_1_out);
endmodule
