// Digital circuit 1bit_MUX.dig as structural Verilog
module _1bit_MUX (
  input  sel,
  input  a,
  input  b,
  output o
);

  wire and_1_out, and_2_out, not_1_out;

  not not_1 (not_1_out, sel);
  and and_1 (and_1_out, a, not_1_out);
  and and_2 (and_2_out, b, sel);
  or or_1 (o, and_1_out, and_2_out);
endmodule
