// Digital circuit 1bit_Register.dig as structural Verilog
module _1bit_Register (
  input  D,
  input  gt_C,
  input  enb,
  output Q
);

  wire and_1_out, pulse_generator_1_o;

  pulse_generator pulse_generator_1 (.i(gt_C), .o(pulse_generator_1_o));
  and and_1 (and_1_out, pulse_generator_1_o, enb);
  D_Latch d_latch_1 (.D(D), .gt_C(and_1_out), .Q(Q));  // open: Q_2
endmodule
