// Digital circuit 1bit_router.dig as structural Verilog
module _1bit_router (
  input  val,
  input  sel,
  output a,
  output b
);

  wire not_1_out;

  not not_1 (not_1_out, sel);
  assign a = not_1_out ? val : 1'bz;  // Driver driver_1
  assign b = sel ? val : 1'bz;  // Driver driver_2
endmodule
