// Digital circuit 256bit_AND.dig as structural Verilog
module _256bit_AND (
  input  [31:0] i_1,
  input  [31:0] i_2,
  input  [31:0] i_3,
  input  [31:0] i_4,
  input  [31:0] i_5,
  input  [31:0] i_6,
  input  [31:0] i_7,
  input  [31:0] i_8,
  input  [31:0] enb,
  output [31:0] o_1,
  output [31:0] o_2,
  output [31:0] o_3,
  output [31:0] o_4,
  output [31:0] o_5,
  output [31:0] o_6,
  output [31:0] o_7,
  output [31:0] o_8
);

  assign o_1 = i_1 & enb;  // And and_1, 32 bits wide
  assign o_2 = i_2 & enb;  // And and_2, 32 bits wide
  assign o_3 = i_3 & enb;  // And and_3, 32 bits wide
  assign o_4 = i_4 & enb;  // And and_4, 32 bits wide
  assign o_5 = i_5 & enb;  // And and_5, 32 bits wide
  assign o_6 = i_6 & enb;  // And and_6, 32 bits wide
  assign o_7 = i_7 & enb;  // And and_7, 32 bits wide
  assign o_8 = i_8 & enb;  // And and_8, 32 bits wide
endmodule
