// Digital circuit 2bit_Decoder.dig as structural Verilog
module _2bit_Decoder (
  input  a,
  input  b,
  output _1,
  output _2,
  output _3,
  output _4
);

  wire not_1_out, not_2_out;

  not not_1 (not_1_out, a);
  not not_2 (not_2_out, b);
  and and_1 (_1, not_1_out, not_2_out);
  and and_2 (_2, a, not_2_out);
  and and_3 (_3, b, not_1_out);
  and and_4 (_4, a, b);
endmodule
