// Digital circuit 32bit_2xMUX.dig as structural Verilog
module _32bit_2xMUX (
  input  sel,
  input  [31:0] a,
  input  [31:0] b,
  output [31:0] o
);

  wire not_1_out;
  wire [31:0] driver_1_out, driver_2_out;

  not not_1 (not_1_out, sel);
  assign driver_1_out = not_1_out ? a : 32'bz;  // Driver driver_1
  PullDown #(.Bits(32)) pulldown_1 (.out(driver_1_out));
  assign driver_2_out = sel ? b : 32'bz;  // Driver driver_2
  PullDown #(.Bits(32)) pulldown_2 (.out(driver_2_out));
  assign o = driver_1_out | driver_2_out;  // Or or_1, 32 bits wide
endmodule
