// Digital circuit 32bit_Adder.dig as structural Verilog
module _32bit_Adder (
  input  [31:0] a,
  input  [31:0] b,
  output [31:0] s,
  output c_out
);

  wire _8bit_adder_1_c_out, _8bit_adder_2_c_out, _8bit_adder_3_c_out;

  _8bit_Adder _8bit_adder_1 (.a(a[7:0]), .b(b[7:0]), .c_in(1'b0), .s(s[7:0]), .c_out(_8bit_adder_1_c_out));
  _8bit_Adder _8bit_adder_2 (
    .a(a[15:8]), .b(b[15:8]), .c_in(_8bit_adder_1_c_out), .s(s[15:8]), .c_out(_8bit_adder_2_c_out));
  _8bit_Adder _8bit_adder_3 (
    .a(a[23:16]), .b(b[23:16]), .c_in(_8bit_adder_2_c_out), .s(s[23:16]), .c_out(_8bit_adder_3_c_out));
  _8bit_Adder _8bit_adder_4 (.a(a[31:24]), .b(b[31:24]), .c_in(_8bit_adder_3_c_out), .s(s[31:24]), .c_out(c_out));
endmodule
