// Digital circuit 32bit_EQ.dig as structural Verilog
module _32bit_EQ (
  input  [31:0] a,
  input  [31:0] b,
  output o
);

  wire [31:0] xor_1_out;

  assign xor_1_out = a ^ b;  // XOr xor_1, 32 bits wide
  or or_1 (o, xor_1_out[0], xor_1_out[1], xor_1_out[2], xor_1_out[3], xor_1_out[4], xor_1_out[5], xor_1_out[6], xor_1_out[7], xor_1_out[8], xor_1_out[9], xor_1_out[10], xor_1_out[11], xor_1_out[12], xor_1_out[13], xor_1_out[14], xor_1_out[15], xor_1_out[16], xor_1_out[17], xor_1_out[18], xor_1_out[19], xor_1_out[20], xor_1_out[21], xor_1_out[22], xor_1_out[23], xor_1_out[24], xor_1_out[25], xor_1_out[26], xor_1_out[27], xor_1_out[28], xor_1_out[29], xor_1_out[30], xor_1_out[31]);
endmodule
