// Digital circuit 32bit_Register.dig as structural Verilog
module _32bit_Register (
  input  gt_C,
  input  [31:0] D,
  input  rd_enb,
  input  rs1_enb,
  input  rs2_enb,
  output [31:0] rs1,
  output [31:0] rs2
);

  wire [7:0] _8bit_register_1_q, _8bit_register_2_q, _8bit_register_3_q, _8bit_register_4_q;

  _8bit_Register _8bit_register_1 (.gt_C(gt_C), .D(D[7:0]), .enb_w(rd_enb), .Q(_8bit_register_1_q));
  _8bit_Register _8bit_register_2 (.gt_C(gt_C), .D(D[15:8]), .enb_w(rd_enb), .Q(_8bit_register_2_q));
  _8bit_Register _8bit_register_3 (.gt_C(gt_C), .D(D[23:16]), .enb_w(rd_enb), .Q(_8bit_register_3_q));
  _8bit_Register _8bit_register_4 (.gt_C(gt_C), .D(D[31:24]), .enb_w(rd_enb), .Q(_8bit_register_4_q));
  assign rs1 = rs1_enb ? {_8bit_register_4_q, _8bit_register_3_q, _8bit_register_2_q, _8bit_register_1_q} : 32'bz;  // Driver driver_1
  assign rs2 = rs2_enb ? {_8bit_register_4_q, _8bit_register_3_q, _8bit_register_2_q, _8bit_register_1_q} : 32'bz;  // Driver driver_2
endmodule
