// Digital circuit 32bit_Sub.dig as structural Verilog
module _32bit_Sub (
  input  [31:0] a,
  input  [31:0] b,
  output [31:0] s,
  output c_out,
  output of
);

  wire _8bit_adder_1_c_out, _8bit_adder_2_c_out, _8bit_adder_3_c_out;
  wire [7:0] xor_1_out, xor_2_out, xor_3_out, xor_4_out;

  assign xor_1_out = {8{1'b1}} ^ b[23:16];  // XOr xor_1, 8 bits wide
  assign xor_2_out = {8{1'b1}} ^ b[31:24];  // XOr xor_2, 8 bits wide
  assign xor_3_out = b[15:8] ^ {8{1'b1}};  // XOr xor_3, 8 bits wide
  assign xor_4_out = b[7:0] ^ {8{1'b1}};  // XOr xor_4, 8 bits wide
  _8bit_Adder _8bit_adder_1 (.a(a[7:0]), .b(xor_4_out), .c_in(1'b1), .s(s[7:0]), .c_out(_8bit_adder_1_c_out));
  _8bit_Adder _8bit_adder_2 (
    .a(a[15:8]), .b(xor_3_out), .c_in(_8bit_adder_1_c_out), .s(s[15:8]), .c_out(_8bit_adder_2_c_out));
  _8bit_Adder _8bit_adder_3 (
    .a(a[23:16]), .b(xor_1_out), .c_in(_8bit_adder_2_c_out), .s(s[23:16]), .c_out(_8bit_adder_3_c_out));
  _8bit_Adder _8bit_adder_4 (.a(a[31:24]), .b(xor_2_out), .c_in(_8bit_adder_3_c_out), .s(s[31:24]), .c_out(c_out));
  nand nand_1 (of, a[31], b[31]);
endmodule
