// Digital circuit 4bit_Router.dig as structural Verilog
module _4bit_Router (
  input  [7:0] a,
  input  [7:0] b,
  input  [7:0] c,
  input  [7:0] d,
  input  [1:0] sel,
  output [7:0] o
);

  wire _2bit_decoder_1__1, _2bit_decoder_1__2, _2bit_decoder_1__3, _2bit_decoder_1__4;

  _2bit_Decoder _2bit_decoder_1 (
    .a(sel[0]), .b(sel[1]), ._1(_2bit_decoder_1__1), ._2(_2bit_decoder_1__2), ._3(_2bit_decoder_1__3),
    ._4(_2bit_decoder_1__4));
  assign o = _2bit_decoder_1__1 ? a : 8'bz;  // Driver driver_1
  assign o = _2bit_decoder_1__2 ? b : 8'bz;  // Driver driver_2
  assign o = _2bit_decoder_1__3 ? c : 8'bz;  // Driver driver_3
  assign o = _2bit_decoder_1__4 ? d : 8'bz;  // Driver driver_4
endmodule
