// Digital circuit 5bit_MUX.dig as structural Verilog
module _5bit_MUX (
  input  [4:0] a,
  output [31:0] o
);

  wire not_1_out, not_2_out, not_3_out, not_4_out, not_5_out;

  not not_1 (not_1_out, a[4]);
  not not_2 (not_2_out, a[2]);
  not not_3 (not_3_out, a[3]);
  not not_4 (not_4_out, a[0]);
  not not_5 (not_5_out, a[1]);
  and and_1 (o[0], not_4_out, not_5_out, not_2_out, not_3_out, not_1_out);
  and and_2 (o[1], a[0], not_5_out, not_2_out, not_3_out, not_1_out);
  and and_3 (o[2], not_4_out, a[1], not_2_out, not_3_out, not_1_out);
  and and_4 (o[3], a[0], a[1], not_2_out, not_3_out, not_1_out);
  and and_5 (o[4], not_4_out, not_5_out, a[2], not_3_out, not_1_out);
  and and_6 (o[5], a[0], not_5_out, a[2], not_3_out, not_1_out);
  and and_7 (o[6], not_4_out, a[1], a[2], not_3_out, not_1_out);
  and and_8 (o[7], a[0], a[1], a[2], not_3_out, not_1_out);
  and and_9 (o[8], not_4_out, not_5_out, not_2_out, a[3], not_1_out);
  and and_10 (o[9], a[0], not_5_out, not_2_out, a[3], not_1_out);
  and and_11 (o[10], not_4_out, a[1], not_2_out, a[3], not_1_out);
  and and_12 (o[11], a[0], a[1], not_2_out, a[3], not_1_out);
  and and_13 (o[12], not_4_out, not_5_out, a[2], a[3], not_1_out);
  and and_14 (o[13], a[0], not_5_out, a[2], a[3], not_1_out);
  and and_15 (o[14], not_4_out, a[1], a[2], a[3], not_1_out);
  and and_16 (o[15], a[0], a[1], a[2], a[3], not_1_out);
  and and_17 (o[16], not_4_out, not_5_out, not_2_out, not_3_out, a[4]);
  and and_18 (o[17], a[0], not_5_out, not_2_out, not_3_out, a[4]);
  and and_19 (o[18], not_4_out, a[1], not_2_out, not_3_out, a[4]);
  and and_20 (o[19], a[0], a[1], not_2_out, not_3_out, a[4]);
  and and_21 (o[20], not_4_out, not_5_out, a[2], not_3_out, a[4]);
  and and_22 (o[21], a[0], not_5_out, a[2], not_3_out, a[4]);
  and and_23 (o[22], not_4_out, a[1], a[2], not_3_out, a[4]);
  and and_24 (o[23], a[0], a[1], a[2], not_3_out, a[4]);
  and and_25 (o[24], not_4_out, not_5_out, not_2_out, a[3], a[4]);
  and and_26 (o[25], a[0], not_5_out, not_2_out, a[3], a[4]);
  and and_27 (o[26], not_4_out, a[1], not_2_out, a[3], a[4]);
  and and_28 (o[27], a[0], a[1], not_2_out, a[3], a[4]);
  and and_29 (o[28], not_4_out, not_5_out, a[2], a[3], a[4]);
  and and_30 (o[29], a[0], not_5_out, a[2], a[3], a[4]);
  and and_31 (o[30], not_4_out, a[1], a[2], a[3], a[4]);
  and and_32 (o[31], a[0], a[1], a[2], a[3], a[4]);
endmodule
