// Digital circuit 8bit_2xMUX.dig as structural Verilog
module _8bit_2xMUX (
  input  sel,
  input  [7:0] a,
  input  [7:0] b,
  output [7:0] o
);

  wire not_1_out;
  wire [7:0] driver_1_out, driver_2_out;

  not not_1 (not_1_out, sel);
  assign driver_1_out = not_1_out ? a : 8'bz;  // Driver driver_1
  PullDown #(.Bits(8)) pulldown_1 (.out(driver_1_out));
  assign driver_2_out = sel ? b : 8'bz;  // Driver driver_2
  PullDown #(.Bits(8)) pulldown_2 (.out(driver_2_out));
  assign o = driver_1_out | driver_2_out;  // Or or_1, 8 bits wide
endmodule
