// Digital circuit 8bit_AND.dig as structural Verilog
module _8bit_AND (
  input  [7:0] i1,
  input  [7:0] i2,
  output [7:0] o
);

  and and_1 (o[0], i1[0], i2[0]);
  and and_2 (o[1], i1[1], i2[1]);
  and and_3 (o[2], i1[2], i2[2]);
  and and_4 (o[3], i1[3], i2[3]);
  and and_5 (o[4], i1[4], i2[4]);
  and and_6 (o[5], i1[5], i2[5]);
  and and_7 (o[6], i1[6], i2[6]);
  and and_8 (o[7], i1[7], i2[7]);
endmodule
