// Digital circuit 8bit_Adder.dig as structural Verilog
module _8bit_Adder (
  input  [7:0] a,
  input  [7:0] b,
  input  c_in,
  output [7:0] s,
  output c_out
);

  wire _1bit_adder_1_c_out, _1bit_adder_2_c_out, _1bit_adder_3_c_out, _1bit_adder_4_c_out,
       _1bit_adder_5_c_out, _1bit_adder_6_c_out, _1bit_adder_7_c_out;

  _1bit_Adder _1bit_adder_1 (.a(a[0]), .b(b[0]), .c_in(c_in), .s(s[0]), .c_out(_1bit_adder_1_c_out));
  _1bit_Adder _1bit_adder_2 (.a(a[1]), .b(b[1]), .c_in(_1bit_adder_1_c_out), .s(s[1]), .c_out(_1bit_adder_2_c_out));
  _1bit_Adder _1bit_adder_3 (.a(a[2]), .b(b[2]), .c_in(_1bit_adder_2_c_out), .s(s[2]), .c_out(_1bit_adder_3_c_out));
  _1bit_Adder _1bit_adder_4 (.a(a[3]), .b(b[3]), .c_in(_1bit_adder_3_c_out), .s(s[3]), .c_out(_1bit_adder_4_c_out));
  _1bit_Adder _1bit_adder_5 (.a(a[4]), .b(b[4]), .c_in(_1bit_adder_4_c_out), .s(s[4]), .c_out(_1bit_adder_5_c_out));
  _1bit_Adder _1bit_adder_6 (.a(a[5]), .b(b[5]), .c_in(_1bit_adder_5_c_out), .s(s[5]), .c_out(_1bit_adder_6_c_out));
  _1bit_Adder _1bit_adder_7 (.a(a[6]), .b(b[6]), .c_in(_1bit_adder_6_c_out), .s(s[6]), .c_out(_1bit_adder_7_c_out));
  _1bit_Adder _1bit_adder_8 (.a(a[7]), .b(b[7]), .c_in(_1bit_adder_7_c_out), .s(s[7]), .c_out(c_out));
endmodule
