// Digital circuit 8bit_Decoder.dig as structural Verilog
module _8bit_Decoder (
  input  [7:0] a,
  output [31:0] _1,
  output [31:0] _2,
  output [31:0] _3,
  output [31:0] _4,
  output [31:0] _5,
  output [31:0] _6,
  output [31:0] _7,
  output [31:0] _8
);

  wire _1_t_t, _2_t_t, _3_t_t, _4_t_t, _5_t_t, _6_t_t, _7_t_t, _8_t_t;

  _1bit_8xAND _1bit_8xand_1 (
    ._1(_1_t_t), ._2(_2_t_t), ._3(_3_t_t), ._4(_4_t_t), ._5(_5_t_t), ._6(_6_t_t), ._7(_7_t_t), ._8(_8_t_t),
    .o(_1[0]));
  _1bit_8xAND _1bit_8xand_2 (
    ._1(a[0]), ._2(_2_t_t), ._3(_3_t_t), ._4(_4_t_t), ._5(_5_t_t), ._6(_6_t_t), ._7(_7_t_t), ._8(_8_t_t),
    .o(_1[1]));
  _1bit_8xAND _1bit_8xand_3 (
    ._1(_1_t_t), ._2(a[1]), ._3(_3_t_t), ._4(_4_t_t), ._5(_5_t_t), ._6(_6_t_t), ._7(_7_t_t), ._8(_8_t_t),
    .o(_1[2]));
  _1bit_8xAND _1bit_8xand_4 (
    ._1(a[0]), ._2(a[1]), ._3(_3_t_t), ._4(_4_t_t), ._5(_5_t_t), ._6(_6_t_t), ._7(_7_t_t), ._8(_8_t_t),
    .o(_1[3]));
  _1bit_8xAND _1bit_8xand_5 (
    ._1(_1_t_t), ._2(_2_t_t), ._3(a[2]), ._4(_4_t_t), ._5(_5_t_t), ._6(_6_t_t), ._7(_7_t_t), ._8(_8_t_t),
    .o(_1[4]));
  _1bit_8xAND _1bit_8xand_6 (
    ._1(a[0]), ._2(_2_t_t), ._3(a[2]), ._4(_4_t_t), ._5(_5_t_t), ._6(_6_t_t), ._7(_7_t_t), ._8(_8_t_t),
    .o(_1[5]));
  _1bit_8xAND _1bit_8xand_7 (
    ._1(_1_t_t), ._2(a[1]), ._3(a[2]), ._4(_4_t_t), ._5(_5_t_t), ._6(_6_t_t), ._7(_7_t_t), ._8(_8_t_t),
    .o(_1[6]));
  _1bit_8xAND _1bit_8xand_8 (
    ._1(a[0]), ._2(a[1]), ._3(a[2]), ._4(_4_t_t), ._5(_5_t_t), ._6(_6_t_t), ._7(_7_t_t), ._8(_8_t_t),
    .o(_1[7]));
  _1bit_8xAND _1bit_8xand_9 (
    ._1(_1_t_t), ._2(_2_t_t), ._3(_3_t_t), ._4(a[3]), ._5(_5_t_t), ._6(_6_t_t), ._7(_7_t_t), ._8(_8_t_t),
    .o(_1[8]));
  _1bit_8xAND _1bit_8xand_10 (
    ._1(a[0]), ._2(_2_t_t), ._3(_3_t_t), ._4(a[3]), ._5(_5_t_t), ._6(_6_t_t), ._7(_7_t_t), ._8(_8_t_t),
    .o(_1[9]));
  _1bit_8xAND _1bit_8xand_11 (
    ._1(_1_t_t), ._2(a[1]), ._3(_3_t_t), ._4(a[3]), ._5(_5_t_t), ._6(_6_t_t), ._7(_7_t_t), ._8(_8_t_t),
    .o(_1[10]));
  _1bit_8xAND _1bit_8xand_12 (
    ._1(a[0]), ._2(a[1]), ._3(_3_t_t), ._4(a[3]), ._5(_5_t_t), ._6(_6_t_t), ._7(_7_t_t), ._8(_8_t_t),
    .o(_1[11]));
  _1bit_8xAND _1bit_8xand_13 (
    ._1(_1_t_t), ._2(_2_t_t), ._3(a[2]), ._4(a[3]), ._5(_5_t_t), ._6(_6_t_t), ._7(_7_t_t), ._8(_8_t_t),
    .o(_1[12]));
  _1bit_8xAND _1bit_8xand_14 (
    ._1(a[0]), ._2(_2_t_t), ._3(a[2]), ._4(a[3]), ._5(_5_t_t), ._6(_6_t_t), ._7(_7_t_t), ._8(_8_t_t),
    .o(_1[13]));
  _1bit_8xAND _1bit_8xand_15 (
    ._1(_1_t_t), ._2(a[1]), ._3(a[2]), ._4(a[3]), ._5(_5_t_t), ._6(_6_t_t), ._7(_7_t_t), ._8(_8_t_t),
    .o(_1[14]));
  _1bit_8xAND _1bit_8xand_16 (
    ._1(a[0]), ._2(a[1]), ._3(a[2]), ._4(a[3]), ._5(_5_t_t), ._6(_6_t_t), ._7(_7_t_t), ._8(_8_t_t), .o(_1[15]));
  _1bit_8xAND _1bit_8xand_17 (
    ._1(_1_t_t), ._2(_2_t_t), ._3(_3_t_t), ._4(_4_t_t), ._5(a[4]), ._6(_6_t_t), ._7(_7_t_t), ._8(_8_t_t),
    .o(_1[16]));
  _1bit_8xAND _1bit_8xand_18 (
    ._1(a[0]), ._2(_2_t_t), ._3(_3_t_t), ._4(_4_t_t), ._5(a[4]), ._6(_6_t_t), ._7(_7_t_t), ._8(_8_t_t),
    .o(_1[17]));
  _1bit_8xAND _1bit_8xand_19 (
    ._1(_1_t_t), ._2(a[1]), ._3(_3_t_t), ._4(_4_t_t), ._5(a[4]), ._6(_6_t_t), ._7(_7_t_t), ._8(_8_t_t),
    .o(_1[18]));
  _1bit_8xAND _1bit_8xand_20 (
    ._1(a[0]), ._2(a[1]), ._3(_3_t_t), ._4(_4_t_t), ._5(a[4]), ._6(_6_t_t), ._7(_7_t_t), ._8(_8_t_t),
    .o(_1[19]));
  _1bit_8xAND _1bit_8xand_21 (
    ._1(_1_t_t), ._2(_2_t_t), ._3(a[2]), ._4(_4_t_t), ._5(a[4]), ._6(_6_t_t), ._7(_7_t_t), ._8(_8_t_t),
    .o(_1[20]));
  _1bit_8xAND _1bit_8xand_22 (
    ._1(a[0]), ._2(_2_t_t), ._3(a[2]), ._4(_4_t_t), ._5(a[4]), ._6(_6_t_t), ._7(_7_t_t), ._8(_8_t_t),
    .o(_1[21]));
  _1bit_8xAND _1bit_8xand_23 (
    ._1(_1_t_t), ._2(a[1]), ._3(a[2]), ._4(_4_t_t), ._5(a[4]), ._6(_6_t_t), ._7(_7_t_t), ._8(_8_t_t),
    .o(_1[22]));
  _1bit_8xAND _1bit_8xand_24 (
    ._1(a[0]), ._2(a[1]), ._3(a[2]), ._4(_4_t_t), ._5(a[4]), ._6(_6_t_t), ._7(_7_t_t), ._8(_8_t_t), .o(_1[23]));
  _1bit_8xAND _1bit_8xand_25 (
    ._1(_1_t_t), ._2(_2_t_t), ._3(_3_t_t), ._4(a[3]), ._5(a[4]), ._6(_6_t_t), ._7(_7_t_t), ._8(_8_t_t),
    .o(_1[24]));
  _1bit_8xAND _1bit_8xand_26 (
    ._1(a[0]), ._2(_2_t_t), ._3(_3_t_t), ._4(a[3]), ._5(a[4]), ._6(_6_t_t), ._7(_7_t_t), ._8(_8_t_t),
    .o(_1[25]));
  _1bit_8xAND _1bit_8xand_27 (
    ._1(_1_t_t), ._2(a[1]), ._3(_3_t_t), ._4(a[3]), ._5(a[4]), ._6(_6_t_t), ._7(_7_t_t), ._8(_8_t_t),
    .o(_1[26]));
  _1bit_8xAND _1bit_8xand_28 (
    ._1(a[0]), ._2(a[1]), ._3(_3_t_t), ._4(a[3]), ._5(a[4]), ._6(_6_t_t), ._7(_7_t_t), ._8(_8_t_t), .o(_1[27]));
  _1bit_8xAND _1bit_8xand_29 (
    ._1(_1_t_t), ._2(_2_t_t), ._3(a[2]), ._4(a[3]), ._5(a[4]), ._6(_6_t_t), ._7(_7_t_t), ._8(_8_t_t),
    .o(_1[28]));
  _1bit_8xAND _1bit_8xand_30 (
    ._1(a[0]), ._2(_2_t_t), ._3(a[2]), ._4(a[3]), ._5(a[4]), ._6(_6_t_t), ._7(_7_t_t), ._8(_8_t_t), .o(_1[29]));
  _1bit_8xAND _1bit_8xand_31 (
    ._1(_1_t_t), ._2(a[1]), ._3(a[2]), ._4(a[3]), ._5(a[4]), ._6(_6_t_t), ._7(_7_t_t), ._8(_8_t_t), .o(_1[30]));
  _1bit_8xAND _1bit_8xand_32 (
    ._1(a[0]), ._2(a[1]), ._3(a[2]), ._4(a[3]), ._5(a[4]), ._6(_6_t_t), ._7(_7_t_t), ._8(_8_t_t), .o(_1[31]));
  _1bit_8xAND _1bit_8xand_33 (
    ._1(_1_t_t), ._2(_2_t_t), ._3(_3_t_t), ._4(_4_t_t), ._5(_5_t_t), ._6(a[5]), ._7(_7_t_t), ._8(_8_t_t),
    .o(_2[0]));
  _1bit_8xAND _1bit_8xand_34 (
    ._1(a[0]), ._2(_2_t_t), ._3(_3_t_t), ._4(_4_t_t), ._5(_5_t_t), ._6(a[5]), ._7(_7_t_t), ._8(_8_t_t),
    .o(_2[1]));
  _1bit_8xAND _1bit_8xand_35 (
    ._1(_1_t_t), ._2(a[1]), ._3(_3_t_t), ._4(_4_t_t), ._5(_5_t_t), ._6(a[5]), ._7(_7_t_t), ._8(_8_t_t),
    .o(_2[2]));
  _1bit_8xAND _1bit_8xand_36 (
    ._1(a[0]), ._2(a[1]), ._3(_3_t_t), ._4(_4_t_t), ._5(_5_t_t), ._6(a[5]), ._7(_7_t_t), ._8(_8_t_t),
    .o(_2[3]));
  _1bit_8xAND _1bit_8xand_37 (
    ._1(_1_t_t), ._2(_2_t_t), ._3(a[2]), ._4(_4_t_t), ._5(_5_t_t), ._6(a[5]), ._7(_7_t_t), ._8(_8_t_t),
    .o(_2[4]));
  _1bit_8xAND _1bit_8xand_38 (
    ._1(a[0]), ._2(_2_t_t), ._3(a[2]), ._4(_4_t_t), ._5(_5_t_t), ._6(a[5]), ._7(_7_t_t), ._8(_8_t_t),
    .o(_2[5]));
  _1bit_8xAND _1bit_8xand_39 (
    ._1(_1_t_t), ._2(a[1]), ._3(a[2]), ._4(_4_t_t), ._5(_5_t_t), ._6(a[5]), ._7(_7_t_t), ._8(_8_t_t),
    .o(_2[6]));
  _1bit_8xAND _1bit_8xand_40 (
    ._1(a[0]), ._2(a[1]), ._3(a[2]), ._4(_4_t_t), ._5(_5_t_t), ._6(a[5]), ._7(_7_t_t), ._8(_8_t_t), .o(_2[7]));
  _1bit_8xAND _1bit_8xand_41 (
    ._1(_1_t_t), ._2(_2_t_t), ._3(_3_t_t), ._4(a[3]), ._5(_5_t_t), ._6(a[5]), ._7(_7_t_t), ._8(_8_t_t),
    .o(_2[8]));
  _1bit_8xAND _1bit_8xand_42 (
    ._1(a[0]), ._2(_2_t_t), ._3(_3_t_t), ._4(a[3]), ._5(_5_t_t), ._6(a[5]), ._7(_7_t_t), ._8(_8_t_t),
    .o(_2[9]));
  _1bit_8xAND _1bit_8xand_43 (
    ._1(_1_t_t), ._2(a[1]), ._3(_3_t_t), ._4(a[3]), ._5(_5_t_t), ._6(a[5]), ._7(_7_t_t), ._8(_8_t_t),
    .o(_2[10]));
  _1bit_8xAND _1bit_8xand_44 (
    ._1(a[0]), ._2(a[1]), ._3(_3_t_t), ._4(a[3]), ._5(_5_t_t), ._6(a[5]), ._7(_7_t_t), ._8(_8_t_t), .o(_2[11]));
  _1bit_8xAND _1bit_8xand_45 (
    ._1(_1_t_t), ._2(_2_t_t), ._3(a[2]), ._4(a[3]), ._5(_5_t_t), ._6(a[5]), ._7(_7_t_t), ._8(_8_t_t),
    .o(_2[12]));
  _1bit_8xAND _1bit_8xand_46 (
    ._1(a[0]), ._2(_2_t_t), ._3(a[2]), ._4(a[3]), ._5(_5_t_t), ._6(a[5]), ._7(_7_t_t), ._8(_8_t_t), .o(_2[13]));
  _1bit_8xAND _1bit_8xand_47 (
    ._1(_1_t_t), ._2(a[1]), ._3(a[2]), ._4(a[3]), ._5(_5_t_t), ._6(a[5]), ._7(_7_t_t), ._8(_8_t_t), .o(_2[14]));
  _1bit_8xAND _1bit_8xand_48 (
    ._1(a[0]), ._2(a[1]), ._3(a[2]), ._4(a[3]), ._5(_5_t_t), ._6(a[5]), ._7(_7_t_t), ._8(_8_t_t), .o(_2[15]));
  _1bit_8xAND _1bit_8xand_49 (
    ._1(_1_t_t), ._2(_2_t_t), ._3(_3_t_t), ._4(_4_t_t), ._5(a[4]), ._6(a[5]), ._7(_7_t_t), ._8(_8_t_t),
    .o(_2[16]));
  _1bit_8xAND _1bit_8xand_50 (
    ._1(a[0]), ._2(_2_t_t), ._3(_3_t_t), ._4(_4_t_t), ._5(a[4]), ._6(a[5]), ._7(_7_t_t), ._8(_8_t_t),
    .o(_2[17]));
  _1bit_8xAND _1bit_8xand_51 (
    ._1(_1_t_t), ._2(a[1]), ._3(_3_t_t), ._4(_4_t_t), ._5(a[4]), ._6(a[5]), ._7(_7_t_t), ._8(_8_t_t),
    .o(_2[18]));
  _1bit_8xAND _1bit_8xand_52 (
    ._1(a[0]), ._2(a[1]), ._3(_3_t_t), ._4(_4_t_t), ._5(a[4]), ._6(a[5]), ._7(_7_t_t), ._8(_8_t_t), .o(_2[19]));
  _1bit_8xAND _1bit_8xand_53 (
    ._1(_1_t_t), ._2(_2_t_t), ._3(a[2]), ._4(_4_t_t), ._5(a[4]), ._6(a[5]), ._7(_7_t_t), ._8(_8_t_t),
    .o(_2[20]));
  _1bit_8xAND _1bit_8xand_54 (
    ._1(a[0]), ._2(_2_t_t), ._3(a[2]), ._4(_4_t_t), ._5(a[4]), ._6(a[5]), ._7(_7_t_t), ._8(_8_t_t), .o(_2[21]));
  _1bit_8xAND _1bit_8xand_55 (
    ._1(_1_t_t), ._2(a[1]), ._3(a[2]), ._4(_4_t_t), ._5(a[4]), ._6(a[5]), ._7(_7_t_t), ._8(_8_t_t), .o(_2[22]));
  _1bit_8xAND _1bit_8xand_56 (
    ._1(a[0]), ._2(a[1]), ._3(a[2]), ._4(_4_t_t), ._5(a[4]), ._6(a[5]), ._7(_7_t_t), ._8(_8_t_t), .o(_2[23]));
  _1bit_8xAND _1bit_8xand_57 (
    ._1(_1_t_t), ._2(_2_t_t), ._3(_3_t_t), ._4(a[3]), ._5(a[4]), ._6(a[5]), ._7(_7_t_t), ._8(_8_t_t),
    .o(_2[24]));
  _1bit_8xAND _1bit_8xand_58 (
    ._1(a[0]), ._2(_2_t_t), ._3(_3_t_t), ._4(a[3]), ._5(a[4]), ._6(a[5]), ._7(_7_t_t), ._8(_8_t_t), .o(_2[25]));
  _1bit_8xAND _1bit_8xand_59 (
    ._1(_1_t_t), ._2(a[1]), ._3(_3_t_t), ._4(a[3]), ._5(a[4]), ._6(a[5]), ._7(_7_t_t), ._8(_8_t_t), .o(_2[26]));
  _1bit_8xAND _1bit_8xand_60 (
    ._1(a[0]), ._2(a[1]), ._3(_3_t_t), ._4(a[3]), ._5(a[4]), ._6(a[5]), ._7(_7_t_t), ._8(_8_t_t), .o(_2[27]));
  _1bit_8xAND _1bit_8xand_61 (
    ._1(_1_t_t), ._2(_2_t_t), ._3(a[2]), ._4(a[3]), ._5(a[4]), ._6(a[5]), ._7(_7_t_t), ._8(_8_t_t), .o(_2[28]));
  _1bit_8xAND _1bit_8xand_62 (
    ._1(a[0]), ._2(_2_t_t), ._3(a[2]), ._4(a[3]), ._5(a[4]), ._6(a[5]), ._7(_7_t_t), ._8(_8_t_t), .o(_2[29]));
  _1bit_8xAND _1bit_8xand_63 (
    ._1(_1_t_t), ._2(a[1]), ._3(a[2]), ._4(a[3]), ._5(a[4]), ._6(a[5]), ._7(_7_t_t), ._8(_8_t_t), .o(_2[30]));
  _1bit_8xAND _1bit_8xand_64 (
    ._1(a[0]), ._2(a[1]), ._3(a[2]), ._4(a[3]), ._5(a[4]), ._6(a[5]), ._7(_7_t_t), ._8(_8_t_t), .o(_2[31]));
  _1bit_8xAND _1bit_8xand_65 (
    ._1(_1_t_t), ._2(_2_t_t), ._3(_3_t_t), ._4(_4_t_t), ._5(_5_t_t), ._6(_6_t_t), ._7(a[6]), ._8(_8_t_t),
    .o(_3[0]));
  _1bit_8xAND _1bit_8xand_66 (
    ._1(a[0]), ._2(_2_t_t), ._3(_3_t_t), ._4(_4_t_t), ._5(_5_t_t), ._6(_6_t_t), ._7(a[6]), ._8(_8_t_t),
    .o(_3[1]));
  _1bit_8xAND _1bit_8xand_67 (
    ._1(_1_t_t), ._2(a[1]), ._3(_3_t_t), ._4(_4_t_t), ._5(_5_t_t), ._6(_6_t_t), ._7(a[6]), ._8(_8_t_t),
    .o(_3[2]));
  _1bit_8xAND _1bit_8xand_68 (
    ._1(a[0]), ._2(a[1]), ._3(_3_t_t), ._4(_4_t_t), ._5(_5_t_t), ._6(_6_t_t), ._7(a[6]), ._8(_8_t_t),
    .o(_3[3]));
  _1bit_8xAND _1bit_8xand_69 (
    ._1(_1_t_t), ._2(_2_t_t), ._3(a[2]), ._4(_4_t_t), ._5(_5_t_t), ._6(_6_t_t), ._7(a[6]), ._8(_8_t_t),
    .o(_3[4]));
  _1bit_8xAND _1bit_8xand_70 (
    ._1(a[0]), ._2(_2_t_t), ._3(a[2]), ._4(_4_t_t), ._5(_5_t_t), ._6(_6_t_t), ._7(a[6]), ._8(_8_t_t),
    .o(_3[5]));
  _1bit_8xAND _1bit_8xand_71 (
    ._1(_1_t_t), ._2(a[1]), ._3(a[2]), ._4(_4_t_t), ._5(_5_t_t), ._6(_6_t_t), ._7(a[6]), ._8(_8_t_t),
    .o(_3[6]));
  _1bit_8xAND _1bit_8xand_72 (
    ._1(a[0]), ._2(a[1]), ._3(a[2]), ._4(_4_t_t), ._5(_5_t_t), ._6(_6_t_t), ._7(a[6]), ._8(_8_t_t), .o(_3[7]));
  _1bit_8xAND _1bit_8xand_73 (
    ._1(_1_t_t), ._2(_2_t_t), ._3(_3_t_t), ._4(a[3]), ._5(_5_t_t), ._6(_6_t_t), ._7(a[6]), ._8(_8_t_t),
    .o(_3[8]));
  _1bit_8xAND _1bit_8xand_74 (
    ._1(a[0]), ._2(_2_t_t), ._3(_3_t_t), ._4(a[3]), ._5(_5_t_t), ._6(_6_t_t), ._7(a[6]), ._8(_8_t_t),
    .o(_3[9]));
  _1bit_8xAND _1bit_8xand_75 (
    ._1(_1_t_t), ._2(a[1]), ._3(_3_t_t), ._4(a[3]), ._5(_5_t_t), ._6(_6_t_t), ._7(a[6]), ._8(_8_t_t),
    .o(_3[10]));
  _1bit_8xAND _1bit_8xand_76 (
    ._1(a[0]), ._2(a[1]), ._3(_3_t_t), ._4(a[3]), ._5(_5_t_t), ._6(_6_t_t), ._7(a[6]), ._8(_8_t_t), .o(_3[11]));
  _1bit_8xAND _1bit_8xand_77 (
    ._1(_1_t_t), ._2(_2_t_t), ._3(a[2]), ._4(a[3]), ._5(_5_t_t), ._6(_6_t_t), ._7(a[6]), ._8(_8_t_t),
    .o(_3[12]));
  _1bit_8xAND _1bit_8xand_78 (
    ._1(a[0]), ._2(_2_t_t), ._3(a[2]), ._4(a[3]), ._5(_5_t_t), ._6(_6_t_t), ._7(a[6]), ._8(_8_t_t), .o(_3[13]));
  _1bit_8xAND _1bit_8xand_79 (
    ._1(_1_t_t), ._2(a[1]), ._3(a[2]), ._4(a[3]), ._5(_5_t_t), ._6(_6_t_t), ._7(a[6]), ._8(_8_t_t), .o(_3[14]));
  _1bit_8xAND _1bit_8xand_80 (
    ._1(a[0]), ._2(a[1]), ._3(a[2]), ._4(a[3]), ._5(_5_t_t), ._6(_6_t_t), ._7(a[6]), ._8(_8_t_t), .o(_3[15]));
  _1bit_8xAND _1bit_8xand_81 (
    ._1(_1_t_t), ._2(_2_t_t), ._3(_3_t_t), ._4(_4_t_t), ._5(a[4]), ._6(_6_t_t), ._7(a[6]), ._8(_8_t_t),
    .o(_3[16]));
  _1bit_8xAND _1bit_8xand_82 (
    ._1(a[0]), ._2(_2_t_t), ._3(_3_t_t), ._4(_4_t_t), ._5(a[4]), ._6(_6_t_t), ._7(a[6]), ._8(_8_t_t),
    .o(_3[17]));
  _1bit_8xAND _1bit_8xand_83 (
    ._1(_1_t_t), ._2(a[1]), ._3(_3_t_t), ._4(_4_t_t), ._5(a[4]), ._6(_6_t_t), ._7(a[6]), ._8(_8_t_t),
    .o(_3[18]));
  _1bit_8xAND _1bit_8xand_84 (
    ._1(a[0]), ._2(a[1]), ._3(_3_t_t), ._4(_4_t_t), ._5(a[4]), ._6(_6_t_t), ._7(a[6]), ._8(_8_t_t), .o(_3[19]));
  _1bit_8xAND _1bit_8xand_85 (
    ._1(_1_t_t), ._2(_2_t_t), ._3(a[2]), ._4(_4_t_t), ._5(a[4]), ._6(_6_t_t), ._7(a[6]), ._8(_8_t_t),
    .o(_3[20]));
  _1bit_8xAND _1bit_8xand_86 (
    ._1(a[0]), ._2(_2_t_t), ._3(a[2]), ._4(_4_t_t), ._5(a[4]), ._6(_6_t_t), ._7(a[6]), ._8(_8_t_t), .o(_3[21]));
  _1bit_8xAND _1bit_8xand_87 (
    ._1(_1_t_t), ._2(a[1]), ._3(a[2]), ._4(_4_t_t), ._5(a[4]), ._6(_6_t_t), ._7(a[6]), ._8(_8_t_t), .o(_3[22]));
  _1bit_8xAND _1bit_8xand_88 (
    ._1(a[0]), ._2(a[1]), ._3(a[2]), ._4(_4_t_t), ._5(a[4]), ._6(_6_t_t), ._7(a[6]), ._8(_8_t_t), .o(_3[23]));
  _1bit_8xAND _1bit_8xand_89 (
    ._1(_1_t_t), ._2(_2_t_t), ._3(_3_t_t), ._4(a[3]), ._5(a[4]), ._6(_6_t_t), ._7(a[6]), ._8(_8_t_t),
    .o(_3[24]));
  _1bit_8xAND _1bit_8xand_90 (
    ._1(a[0]), ._2(_2_t_t), ._3(_3_t_t), ._4(a[3]), ._5(a[4]), ._6(_6_t_t), ._7(a[6]), ._8(_8_t_t), .o(_3[25]));
  _1bit_8xAND _1bit_8xand_91 (
    ._1(_1_t_t), ._2(a[1]), ._3(_3_t_t), ._4(a[3]), ._5(a[4]), ._6(_6_t_t), ._7(a[6]), ._8(_8_t_t), .o(_3[26]));
  _1bit_8xAND _1bit_8xand_92 (
    ._1(a[0]), ._2(a[1]), ._3(_3_t_t), ._4(a[3]), ._5(a[4]), ._6(_6_t_t), ._7(a[6]), ._8(_8_t_t), .o(_3[27]));
  _1bit_8xAND _1bit_8xand_93 (
    ._1(_1_t_t), ._2(_2_t_t), ._3(a[2]), ._4(a[3]), ._5(a[4]), ._6(_6_t_t), ._7(a[6]), ._8(_8_t_t), .o(_3[28]));
  _1bit_8xAND _1bit_8xand_94 (
    ._1(a[0]), ._2(_2_t_t), ._3(a[2]), ._4(a[3]), ._5(a[4]), ._6(_6_t_t), ._7(a[6]), ._8(_8_t_t), .o(_3[29]));
  _1bit_8xAND _1bit_8xand_95 (
    ._1(_1_t_t), ._2(a[1]), ._3(a[2]), ._4(a[3]), ._5(a[4]), ._6(_6_t_t), ._7(a[6]), ._8(_8_t_t), .o(_3[30]));
  _1bit_8xAND _1bit_8xand_96 (
    ._1(a[0]), ._2(a[1]), ._3(a[2]), ._4(a[3]), ._5(a[4]), ._6(_6_t_t), ._7(a[6]), ._8(_8_t_t), .o(_3[31]));
  _1bit_8xAND _1bit_8xand_97 (
    ._1(_1_t_t), ._2(_2_t_t), ._3(_3_t_t), ._4(_4_t_t), ._5(_5_t_t), ._6(a[5]), ._7(a[6]), ._8(_8_t_t),
    .o(_4[0]));
  _1bit_8xAND _1bit_8xand_98 (
    ._1(a[0]), ._2(_2_t_t), ._3(_3_t_t), ._4(_4_t_t), ._5(_5_t_t), ._6(a[5]), ._7(a[6]), ._8(_8_t_t),
    .o(_4[1]));
  _1bit_8xAND _1bit_8xand_99 (
    ._1(_1_t_t), ._2(a[1]), ._3(_3_t_t), ._4(_4_t_t), ._5(_5_t_t), ._6(a[5]), ._7(a[6]), ._8(_8_t_t),
    .o(_4[2]));
  _1bit_8xAND _1bit_8xand_100 (
    ._1(a[0]), ._2(a[1]), ._3(_3_t_t), ._4(_4_t_t), ._5(_5_t_t), ._6(a[5]), ._7(a[6]), ._8(_8_t_t), .o(_4[3]));
  _1bit_8xAND _1bit_8xand_101 (
    ._1(_1_t_t), ._2(_2_t_t), ._3(a[2]), ._4(_4_t_t), ._5(_5_t_t), ._6(a[5]), ._7(a[6]), ._8(_8_t_t),
    .o(_4[4]));
  _1bit_8xAND _1bit_8xand_102 (
    ._1(a[0]), ._2(_2_t_t), ._3(a[2]), ._4(_4_t_t), ._5(_5_t_t), ._6(a[5]), ._7(a[6]), ._8(_8_t_t), .o(_4[5]));
  _1bit_8xAND _1bit_8xand_103 (
    ._1(_1_t_t), ._2(a[1]), ._3(a[2]), ._4(_4_t_t), ._5(_5_t_t), ._6(a[5]), ._7(a[6]), ._8(_8_t_t), .o(_4[6]));
  _1bit_8xAND _1bit_8xand_104 (
    ._1(a[0]), ._2(a[1]), ._3(a[2]), ._4(_4_t_t), ._5(_5_t_t), ._6(a[5]), ._7(a[6]), ._8(_8_t_t), .o(_4[7]));
  _1bit_8xAND _1bit_8xand_105 (
    ._1(_1_t_t), ._2(_2_t_t), ._3(_3_t_t), ._4(a[3]), ._5(_5_t_t), ._6(a[5]), ._7(a[6]), ._8(_8_t_t),
    .o(_4[8]));
  _1bit_8xAND _1bit_8xand_106 (
    ._1(a[0]), ._2(_2_t_t), ._3(_3_t_t), ._4(a[3]), ._5(_5_t_t), ._6(a[5]), ._7(a[6]), ._8(_8_t_t), .o(_4[9]));
  _1bit_8xAND _1bit_8xand_107 (
    ._1(_1_t_t), ._2(a[1]), ._3(_3_t_t), ._4(a[3]), ._5(_5_t_t), ._6(a[5]), ._7(a[6]), ._8(_8_t_t), .o(_4[10]));
  _1bit_8xAND _1bit_8xand_108 (
    ._1(a[0]), ._2(a[1]), ._3(_3_t_t), ._4(a[3]), ._5(_5_t_t), ._6(a[5]), ._7(a[6]), ._8(_8_t_t), .o(_4[11]));
  _1bit_8xAND _1bit_8xand_109 (
    ._1(_1_t_t), ._2(_2_t_t), ._3(a[2]), ._4(a[3]), ._5(_5_t_t), ._6(a[5]), ._7(a[6]), ._8(_8_t_t), .o(_4[12]));
  _1bit_8xAND _1bit_8xand_110 (
    ._1(a[0]), ._2(_2_t_t), ._3(a[2]), ._4(a[3]), ._5(_5_t_t), ._6(a[5]), ._7(a[6]), ._8(_8_t_t), .o(_4[13]));
  _1bit_8xAND _1bit_8xand_111 (
    ._1(_1_t_t), ._2(a[1]), ._3(a[2]), ._4(a[3]), ._5(_5_t_t), ._6(a[5]), ._7(a[6]), ._8(_8_t_t), .o(_4[14]));
  _1bit_8xAND _1bit_8xand_112 (
    ._1(a[0]), ._2(a[1]), ._3(a[2]), ._4(a[3]), ._5(_5_t_t), ._6(a[5]), ._7(a[6]), ._8(_8_t_t), .o(_4[15]));
  _1bit_8xAND _1bit_8xand_113 (
    ._1(_1_t_t), ._2(_2_t_t), ._3(_3_t_t), ._4(_4_t_t), ._5(a[4]), ._6(a[5]), ._7(a[6]), ._8(_8_t_t),
    .o(_4[16]));
  _1bit_8xAND _1bit_8xand_114 (
    ._1(a[0]), ._2(_2_t_t), ._3(_3_t_t), ._4(_4_t_t), ._5(a[4]), ._6(a[5]), ._7(a[6]), ._8(_8_t_t), .o(_4[17]));
  _1bit_8xAND _1bit_8xand_115 (
    ._1(_1_t_t), ._2(a[1]), ._3(_3_t_t), ._4(_4_t_t), ._5(a[4]), ._6(a[5]), ._7(a[6]), ._8(_8_t_t), .o(_4[18]));
  _1bit_8xAND _1bit_8xand_116 (
    ._1(a[0]), ._2(a[1]), ._3(_3_t_t), ._4(_4_t_t), ._5(a[4]), ._6(a[5]), ._7(a[6]), ._8(_8_t_t), .o(_4[19]));
  _1bit_8xAND _1bit_8xand_117 (
    ._1(_1_t_t), ._2(_2_t_t), ._3(a[2]), ._4(_4_t_t), ._5(a[4]), ._6(a[5]), ._7(a[6]), ._8(_8_t_t), .o(_4[20]));
  _1bit_8xAND _1bit_8xand_118 (
    ._1(a[0]), ._2(_2_t_t), ._3(a[2]), ._4(_4_t_t), ._5(a[4]), ._6(a[5]), ._7(a[6]), ._8(_8_t_t), .o(_4[21]));
  _1bit_8xAND _1bit_8xand_119 (
    ._1(_1_t_t), ._2(a[1]), ._3(a[2]), ._4(_4_t_t), ._5(a[4]), ._6(a[5]), ._7(a[6]), ._8(_8_t_t), .o(_4[22]));
  _1bit_8xAND _1bit_8xand_120 (
    ._1(a[0]), ._2(a[1]), ._3(a[2]), ._4(_4_t_t), ._5(a[4]), ._6(a[5]), ._7(a[6]), ._8(_8_t_t), .o(_4[23]));
  _1bit_8xAND _1bit_8xand_121 (
    ._1(_1_t_t), ._2(_2_t_t), ._3(_3_t_t), ._4(a[3]), ._5(a[4]), ._6(a[5]), ._7(a[6]), ._8(_8_t_t), .o(_4[24]));
  _1bit_8xAND _1bit_8xand_122 (
    ._1(a[0]), ._2(_2_t_t), ._3(_3_t_t), ._4(a[3]), ._5(a[4]), ._6(a[5]), ._7(a[6]), ._8(_8_t_t), .o(_4[25]));
  _1bit_8xAND _1bit_8xand_123 (
    ._1(_1_t_t), ._2(a[1]), ._3(_3_t_t), ._4(a[3]), ._5(a[4]), ._6(a[5]), ._7(a[6]), ._8(_8_t_t), .o(_4[26]));
  _1bit_8xAND _1bit_8xand_124 (
    ._1(a[0]), ._2(a[1]), ._3(_3_t_t), ._4(a[3]), ._5(a[4]), ._6(a[5]), ._7(a[6]), ._8(_8_t_t), .o(_4[27]));
  _1bit_8xAND _1bit_8xand_125 (
    ._1(_1_t_t), ._2(_2_t_t), ._3(a[2]), ._4(a[3]), ._5(a[4]), ._6(a[5]), ._7(a[6]), ._8(_8_t_t), .o(_4[28]));
  _1bit_8xAND _1bit_8xand_126 (
    ._1(a[0]), ._2(_2_t_t), ._3(a[2]), ._4(a[3]), ._5(a[4]), ._6(a[5]), ._7(a[6]), ._8(_8_t_t), .o(_4[29]));
  _1bit_8xAND _1bit_8xand_127 (
    ._1(_1_t_t), ._2(a[1]), ._3(a[2]), ._4(a[3]), ._5(a[4]), ._6(a[5]), ._7(a[6]), ._8(_8_t_t), .o(_4[30]));
  _1bit_8xAND _1bit_8xand_128 (
    ._1(a[0]), ._2(a[1]), ._3(a[2]), ._4(a[3]), ._5(a[4]), ._6(a[5]), ._7(a[6]), ._8(_8_t_t), .o(_4[31]));
  not not_1 (_1_t_t, a[0]);
  not not_2 (_3_t_t, a[2]);
  not not_3 (_2_t_t, a[1]);
  not not_4 (_4_t_t, a[3]);
  not not_5 (_5_t_t, a[4]);
  not not_6 (_6_t_t, a[5]);
  not not_7 (_7_t_t, a[6]);
  not not_8 (_8_t_t, a[7]);
  _1bit_8xAND _1bit_8xand_129 (
    ._1(_1_t_t), ._2(_2_t_t), ._3(_3_t_t), ._4(_4_t_t), ._5(_5_t_t), ._6(_6_t_t), ._7(_7_t_t), ._8(a[7]),
    .o(_5[0]));
  _1bit_8xAND _1bit_8xand_130 (
    ._1(a[0]), ._2(_2_t_t), ._3(_3_t_t), ._4(_4_t_t), ._5(_5_t_t), ._6(_6_t_t), ._7(_7_t_t), ._8(a[7]),
    .o(_5[1]));
  _1bit_8xAND _1bit_8xand_131 (
    ._1(_1_t_t), ._2(a[1]), ._3(_3_t_t), ._4(_4_t_t), ._5(_5_t_t), ._6(_6_t_t), ._7(_7_t_t), ._8(a[7]),
    .o(_5[2]));
  _1bit_8xAND _1bit_8xand_132 (
    ._1(a[0]), ._2(a[1]), ._3(_3_t_t), ._4(_4_t_t), ._5(_5_t_t), ._6(_6_t_t), ._7(_7_t_t), ._8(a[7]),
    .o(_5[3]));
  _1bit_8xAND _1bit_8xand_133 (
    ._1(_1_t_t), ._2(_2_t_t), ._3(a[2]), ._4(_4_t_t), ._5(_5_t_t), ._6(_6_t_t), ._7(_7_t_t), ._8(a[7]),
    .o(_5[4]));
  _1bit_8xAND _1bit_8xand_134 (
    ._1(a[0]), ._2(_2_t_t), ._3(a[2]), ._4(_4_t_t), ._5(_5_t_t), ._6(_6_t_t), ._7(_7_t_t), ._8(a[7]),
    .o(_5[5]));
  _1bit_8xAND _1bit_8xand_135 (
    ._1(_1_t_t), ._2(a[1]), ._3(a[2]), ._4(_4_t_t), ._5(_5_t_t), ._6(_6_t_t), ._7(_7_t_t), ._8(a[7]),
    .o(_5[6]));
  _1bit_8xAND _1bit_8xand_136 (
    ._1(a[0]), ._2(a[1]), ._3(a[2]), ._4(_4_t_t), ._5(_5_t_t), ._6(_6_t_t), ._7(_7_t_t), ._8(a[7]), .o(_5[7]));
  _1bit_8xAND _1bit_8xand_137 (
    ._1(_1_t_t), ._2(_2_t_t), ._3(_3_t_t), ._4(a[3]), ._5(_5_t_t), ._6(_6_t_t), ._7(_7_t_t), ._8(a[7]),
    .o(_5[8]));
  _1bit_8xAND _1bit_8xand_138 (
    ._1(a[0]), ._2(_2_t_t), ._3(_3_t_t), ._4(a[3]), ._5(_5_t_t), ._6(_6_t_t), ._7(_7_t_t), ._8(a[7]),
    .o(_5[9]));
  _1bit_8xAND _1bit_8xand_139 (
    ._1(_1_t_t), ._2(a[1]), ._3(_3_t_t), ._4(a[3]), ._5(_5_t_t), ._6(_6_t_t), ._7(_7_t_t), ._8(a[7]),
    .o(_5[10]));
  _1bit_8xAND _1bit_8xand_140 (
    ._1(a[0]), ._2(a[1]), ._3(_3_t_t), ._4(a[3]), ._5(_5_t_t), ._6(_6_t_t), ._7(_7_t_t), ._8(a[7]), .o(_5[11]));
  _1bit_8xAND _1bit_8xand_141 (
    ._1(_1_t_t), ._2(_2_t_t), ._3(a[2]), ._4(a[3]), ._5(_5_t_t), ._6(_6_t_t), ._7(_7_t_t), ._8(a[7]),
    .o(_5[12]));
  _1bit_8xAND _1bit_8xand_142 (
    ._1(a[0]), ._2(_2_t_t), ._3(a[2]), ._4(a[3]), ._5(_5_t_t), ._6(_6_t_t), ._7(_7_t_t), ._8(a[7]), .o(_5[13]));
  _1bit_8xAND _1bit_8xand_143 (
    ._1(_1_t_t), ._2(a[1]), ._3(a[2]), ._4(a[3]), ._5(_5_t_t), ._6(_6_t_t), ._7(_7_t_t), ._8(a[7]), .o(_5[14]));
  _1bit_8xAND _1bit_8xand_144 (
    ._1(a[0]), ._2(a[1]), ._3(a[2]), ._4(a[3]), ._5(_5_t_t), ._6(_6_t_t), ._7(_7_t_t), ._8(a[7]), .o(_5[15]));
  _1bit_8xAND _1bit_8xand_145 (
    ._1(_1_t_t), ._2(_2_t_t), ._3(_3_t_t), ._4(_4_t_t), ._5(a[4]), ._6(_6_t_t), ._7(_7_t_t), ._8(a[7]),
    .o(_5[16]));
  _1bit_8xAND _1bit_8xand_146 (
    ._1(a[0]), ._2(_2_t_t), ._3(_3_t_t), ._4(_4_t_t), ._5(a[4]), ._6(_6_t_t), ._7(_7_t_t), ._8(a[7]),
    .o(_5[17]));
  _1bit_8xAND _1bit_8xand_147 (
    ._1(_1_t_t), ._2(a[1]), ._3(_3_t_t), ._4(_4_t_t), ._5(a[4]), ._6(_6_t_t), ._7(_7_t_t), ._8(a[7]),
    .o(_5[18]));
  _1bit_8xAND _1bit_8xand_148 (
    ._1(a[0]), ._2(a[1]), ._3(_3_t_t), ._4(_4_t_t), ._5(a[4]), ._6(_6_t_t), ._7(_7_t_t), ._8(a[7]), .o(_5[19]));
  _1bit_8xAND _1bit_8xand_149 (
    ._1(_1_t_t), ._2(_2_t_t), ._3(a[2]), ._4(_4_t_t), ._5(a[4]), ._6(_6_t_t), ._7(_7_t_t), ._8(a[7]),
    .o(_5[20]));
  _1bit_8xAND _1bit_8xand_150 (
    ._1(a[0]), ._2(_2_t_t), ._3(a[2]), ._4(_4_t_t), ._5(a[4]), ._6(_6_t_t), ._7(_7_t_t), ._8(a[7]), .o(_5[21]));
  _1bit_8xAND _1bit_8xand_151 (
    ._1(_1_t_t), ._2(a[1]), ._3(a[2]), ._4(_4_t_t), ._5(a[4]), ._6(_6_t_t), ._7(_7_t_t), ._8(a[7]), .o(_5[22]));
  _1bit_8xAND _1bit_8xand_152 (
    ._1(a[0]), ._2(a[1]), ._3(a[2]), ._4(_4_t_t), ._5(a[4]), ._6(_6_t_t), ._7(_7_t_t), ._8(a[7]), .o(_5[23]));
  _1bit_8xAND _1bit_8xand_153 (
    ._1(_1_t_t), ._2(_2_t_t), ._3(_3_t_t), ._4(a[3]), ._5(a[4]), ._6(_6_t_t), ._7(_7_t_t), ._8(a[7]),
    .o(_5[24]));
  _1bit_8xAND _1bit_8xand_154 (
    ._1(a[0]), ._2(_2_t_t), ._3(_3_t_t), ._4(a[3]), ._5(a[4]), ._6(_6_t_t), ._7(_7_t_t), ._8(a[7]), .o(_5[25]));
  _1bit_8xAND _1bit_8xand_155 (
    ._1(_1_t_t), ._2(a[1]), ._3(_3_t_t), ._4(a[3]), ._5(a[4]), ._6(_6_t_t), ._7(_7_t_t), ._8(a[7]), .o(_5[26]));
  _1bit_8xAND _1bit_8xand_156 (
    ._1(a[0]), ._2(a[1]), ._3(_3_t_t), ._4(a[3]), ._5(a[4]), ._6(_6_t_t), ._7(_7_t_t), ._8(a[7]), .o(_5[27]));
  _1bit_8xAND _1bit_8xand_157 (
    ._1(_1_t_t), ._2(_2_t_t), ._3(a[2]), ._4(a[3]), ._5(a[4]), ._6(_6_t_t), ._7(_7_t_t), ._8(a[7]), .o(_5[28]));
  _1bit_8xAND _1bit_8xand_158 (
    ._1(a[0]), ._2(_2_t_t), ._3(a[2]), ._4(a[3]), ._5(a[4]), ._6(_6_t_t), ._7(_7_t_t), ._8(a[7]), .o(_5[29]));
  _1bit_8xAND _1bit_8xand_159 (
    ._1(_1_t_t), ._2(a[1]), ._3(a[2]), ._4(a[3]), ._5(a[4]), ._6(_6_t_t), ._7(_7_t_t), ._8(a[7]), .o(_5[30]));
  _1bit_8xAND _1bit_8xand_160 (
    ._1(a[0]), ._2(a[1]), ._3(a[2]), ._4(a[3]), ._5(a[4]), ._6(_6_t_t), ._7(_7_t_t), ._8(a[7]), .o(_5[31]));
  _1bit_8xAND _1bit_8xand_161 (
    ._1(_1_t_t), ._2(_2_t_t), ._3(_3_t_t), ._4(_4_t_t), ._5(_5_t_t), ._6(a[5]), ._7(_7_t_t), ._8(a[7]),
    .o(_6[0]));
  _1bit_8xAND _1bit_8xand_162 (
    ._1(a[0]), ._2(_2_t_t), ._3(_3_t_t), ._4(_4_t_t), ._5(_5_t_t), ._6(a[5]), ._7(_7_t_t), ._8(a[7]),
    .o(_6[1]));
  _1bit_8xAND _1bit_8xand_163 (
    ._1(_1_t_t), ._2(a[1]), ._3(_3_t_t), ._4(_4_t_t), ._5(_5_t_t), ._6(a[5]), ._7(_7_t_t), ._8(a[7]),
    .o(_6[2]));
  _1bit_8xAND _1bit_8xand_164 (
    ._1(a[0]), ._2(a[1]), ._3(_3_t_t), ._4(_4_t_t), ._5(_5_t_t), ._6(a[5]), ._7(_7_t_t), ._8(a[7]), .o(_6[3]));
  _1bit_8xAND _1bit_8xand_165 (
    ._1(_1_t_t), ._2(_2_t_t), ._3(a[2]), ._4(_4_t_t), ._5(_5_t_t), ._6(a[5]), ._7(_7_t_t), ._8(a[7]),
    .o(_6[4]));
  _1bit_8xAND _1bit_8xand_166 (
    ._1(a[0]), ._2(_2_t_t), ._3(a[2]), ._4(_4_t_t), ._5(_5_t_t), ._6(a[5]), ._7(_7_t_t), ._8(a[7]), .o(_6[5]));
  _1bit_8xAND _1bit_8xand_167 (
    ._1(_1_t_t), ._2(a[1]), ._3(a[2]), ._4(_4_t_t), ._5(_5_t_t), ._6(a[5]), ._7(_7_t_t), ._8(a[7]), .o(_6[6]));
  _1bit_8xAND _1bit_8xand_168 (
    ._1(a[0]), ._2(a[1]), ._3(a[2]), ._4(_4_t_t), ._5(_5_t_t), ._6(a[5]), ._7(_7_t_t), ._8(a[7]), .o(_6[7]));
  _1bit_8xAND _1bit_8xand_169 (
    ._1(_1_t_t), ._2(_2_t_t), ._3(_3_t_t), ._4(a[3]), ._5(_5_t_t), ._6(a[5]), ._7(_7_t_t), ._8(a[7]),
    .o(_6[8]));
  _1bit_8xAND _1bit_8xand_170 (
    ._1(a[0]), ._2(_2_t_t), ._3(_3_t_t), ._4(a[3]), ._5(_5_t_t), ._6(a[5]), ._7(_7_t_t), ._8(a[7]), .o(_6[9]));
  _1bit_8xAND _1bit_8xand_171 (
    ._1(_1_t_t), ._2(a[1]), ._3(_3_t_t), ._4(a[3]), ._5(_5_t_t), ._6(a[5]), ._7(_7_t_t), ._8(a[7]), .o(_6[10]));
  _1bit_8xAND _1bit_8xand_172 (
    ._1(a[0]), ._2(a[1]), ._3(_3_t_t), ._4(a[3]), ._5(_5_t_t), ._6(a[5]), ._7(_7_t_t), ._8(a[7]), .o(_6[11]));
  _1bit_8xAND _1bit_8xand_173 (
    ._1(_1_t_t), ._2(_2_t_t), ._3(a[2]), ._4(a[3]), ._5(_5_t_t), ._6(a[5]), ._7(_7_t_t), ._8(a[7]), .o(_6[12]));
  _1bit_8xAND _1bit_8xand_174 (
    ._1(a[0]), ._2(_2_t_t), ._3(a[2]), ._4(a[3]), ._5(_5_t_t), ._6(a[5]), ._7(_7_t_t), ._8(a[7]), .o(_6[13]));
  _1bit_8xAND _1bit_8xand_175 (
    ._1(_1_t_t), ._2(a[1]), ._3(a[2]), ._4(a[3]), ._5(_5_t_t), ._6(a[5]), ._7(_7_t_t), ._8(a[7]), .o(_6[14]));
  _1bit_8xAND _1bit_8xand_176 (
    ._1(a[0]), ._2(a[1]), ._3(a[2]), ._4(a[3]), ._5(_5_t_t), ._6(a[5]), ._7(_7_t_t), ._8(a[7]), .o(_6[15]));
  _1bit_8xAND _1bit_8xand_177 (
    ._1(_1_t_t), ._2(_2_t_t), ._3(_3_t_t), ._4(_4_t_t), ._5(a[4]), ._6(a[5]), ._7(_7_t_t), ._8(a[7]),
    .o(_6[16]));
  _1bit_8xAND _1bit_8xand_178 (
    ._1(a[0]), ._2(_2_t_t), ._3(_3_t_t), ._4(_4_t_t), ._5(a[4]), ._6(a[5]), ._7(_7_t_t), ._8(a[7]), .o(_6[17]));
  _1bit_8xAND _1bit_8xand_179 (
    ._1(_1_t_t), ._2(a[1]), ._3(_3_t_t), ._4(_4_t_t), ._5(a[4]), ._6(a[5]), ._7(_7_t_t), ._8(a[7]), .o(_6[18]));
  _1bit_8xAND _1bit_8xand_180 (
    ._1(a[0]), ._2(a[1]), ._3(_3_t_t), ._4(_4_t_t), ._5(a[4]), ._6(a[5]), ._7(_7_t_t), ._8(a[7]), .o(_6[19]));
  _1bit_8xAND _1bit_8xand_181 (
    ._1(_1_t_t), ._2(_2_t_t), ._3(a[2]), ._4(_4_t_t), ._5(a[4]), ._6(a[5]), ._7(_7_t_t), ._8(a[7]), .o(_6[20]));
  _1bit_8xAND _1bit_8xand_182 (
    ._1(a[0]), ._2(_2_t_t), ._3(a[2]), ._4(_4_t_t), ._5(a[4]), ._6(a[5]), ._7(_7_t_t), ._8(a[7]), .o(_6[21]));
  _1bit_8xAND _1bit_8xand_183 (
    ._1(_1_t_t), ._2(a[1]), ._3(a[2]), ._4(_4_t_t), ._5(a[4]), ._6(a[5]), ._7(_7_t_t), ._8(a[7]), .o(_6[22]));
  _1bit_8xAND _1bit_8xand_184 (
    ._1(a[0]), ._2(a[1]), ._3(a[2]), ._4(_4_t_t), ._5(a[4]), ._6(a[5]), ._7(_7_t_t), ._8(a[7]), .o(_6[23]));
  _1bit_8xAND _1bit_8xand_185 (
    ._1(_1_t_t), ._2(_2_t_t), ._3(_3_t_t), ._4(a[3]), ._5(a[4]), ._6(a[5]), ._7(_7_t_t), ._8(a[7]), .o(_6[24]));
  _1bit_8xAND _1bit_8xand_186 (
    ._1(a[0]), ._2(_2_t_t), ._3(_3_t_t), ._4(a[3]), ._5(a[4]), ._6(a[5]), ._7(_7_t_t), ._8(a[7]), .o(_6[25]));
  _1bit_8xAND _1bit_8xand_187 (
    ._1(_1_t_t), ._2(a[1]), ._3(_3_t_t), ._4(a[3]), ._5(a[4]), ._6(a[5]), ._7(_7_t_t), ._8(a[7]), .o(_6[26]));
  _1bit_8xAND _1bit_8xand_188 (
    ._1(a[0]), ._2(a[1]), ._3(_3_t_t), ._4(a[3]), ._5(a[4]), ._6(a[5]), ._7(_7_t_t), ._8(a[7]), .o(_6[27]));
  _1bit_8xAND _1bit_8xand_189 (
    ._1(_1_t_t), ._2(_2_t_t), ._3(a[2]), ._4(a[3]), ._5(a[4]), ._6(a[5]), ._7(_7_t_t), ._8(a[7]), .o(_6[28]));
  _1bit_8xAND _1bit_8xand_190 (
    ._1(a[0]), ._2(_2_t_t), ._3(a[2]), ._4(a[3]), ._5(a[4]), ._6(a[5]), ._7(_7_t_t), ._8(a[7]), .o(_6[29]));
  _1bit_8xAND _1bit_8xand_191 (
    ._1(_1_t_t), ._2(a[1]), ._3(a[2]), ._4(a[3]), ._5(a[4]), ._6(a[5]), ._7(_7_t_t), ._8(a[7]), .o(_6[30]));
  _1bit_8xAND _1bit_8xand_192 (
    ._1(a[0]), ._2(a[1]), ._3(a[2]), ._4(a[3]), ._5(a[4]), ._6(a[5]), ._7(_7_t_t), ._8(a[7]), .o(_6[31]));
  _1bit_8xAND _1bit_8xand_193 (
    ._1(_1_t_t), ._2(_2_t_t), ._3(_3_t_t), ._4(_4_t_t), ._5(_5_t_t), ._6(_6_t_t), ._7(a[6]), ._8(a[7]),
    .o(_7[0]));
  _1bit_8xAND _1bit_8xand_194 (
    ._1(a[0]), ._2(_2_t_t), ._3(_3_t_t), ._4(_4_t_t), ._5(_5_t_t), ._6(_6_t_t), ._7(a[6]), ._8(a[7]),
    .o(_7[1]));
  _1bit_8xAND _1bit_8xand_195 (
    ._1(_1_t_t), ._2(a[1]), ._3(_3_t_t), ._4(_4_t_t), ._5(_5_t_t), ._6(_6_t_t), ._7(a[6]), ._8(a[7]),
    .o(_7[2]));
  _1bit_8xAND _1bit_8xand_196 (
    ._1(a[0]), ._2(a[1]), ._3(_3_t_t), ._4(_4_t_t), ._5(_5_t_t), ._6(_6_t_t), ._7(a[6]), ._8(a[7]), .o(_7[3]));
  _1bit_8xAND _1bit_8xand_197 (
    ._1(_1_t_t), ._2(_2_t_t), ._3(a[2]), ._4(_4_t_t), ._5(_5_t_t), ._6(_6_t_t), ._7(a[6]), ._8(a[7]),
    .o(_7[4]));
  _1bit_8xAND _1bit_8xand_198 (
    ._1(a[0]), ._2(_2_t_t), ._3(a[2]), ._4(_4_t_t), ._5(_5_t_t), ._6(_6_t_t), ._7(a[6]), ._8(a[7]), .o(_7[5]));
  _1bit_8xAND _1bit_8xand_199 (
    ._1(_1_t_t), ._2(a[1]), ._3(a[2]), ._4(_4_t_t), ._5(_5_t_t), ._6(_6_t_t), ._7(a[6]), ._8(a[7]), .o(_7[6]));
  _1bit_8xAND _1bit_8xand_200 (
    ._1(a[0]), ._2(a[1]), ._3(a[2]), ._4(_4_t_t), ._5(_5_t_t), ._6(_6_t_t), ._7(a[6]), ._8(a[7]), .o(_7[7]));
  _1bit_8xAND _1bit_8xand_201 (
    ._1(_1_t_t), ._2(_2_t_t), ._3(_3_t_t), ._4(a[3]), ._5(_5_t_t), ._6(_6_t_t), ._7(a[6]), ._8(a[7]),
    .o(_7[8]));
  _1bit_8xAND _1bit_8xand_202 (
    ._1(a[0]), ._2(_2_t_t), ._3(_3_t_t), ._4(a[3]), ._5(_5_t_t), ._6(_6_t_t), ._7(a[6]), ._8(a[7]), .o(_7[9]));
  _1bit_8xAND _1bit_8xand_203 (
    ._1(_1_t_t), ._2(a[1]), ._3(_3_t_t), ._4(a[3]), ._5(_5_t_t), ._6(_6_t_t), ._7(a[6]), ._8(a[7]), .o(_7[10]));
  _1bit_8xAND _1bit_8xand_204 (
    ._1(a[0]), ._2(a[1]), ._3(_3_t_t), ._4(a[3]), ._5(_5_t_t), ._6(_6_t_t), ._7(a[6]), ._8(a[7]), .o(_7[11]));
  _1bit_8xAND _1bit_8xand_205 (
    ._1(_1_t_t), ._2(_2_t_t), ._3(a[2]), ._4(a[3]), ._5(_5_t_t), ._6(_6_t_t), ._7(a[6]), ._8(a[7]), .o(_7[12]));
  _1bit_8xAND _1bit_8xand_206 (
    ._1(a[0]), ._2(_2_t_t), ._3(a[2]), ._4(a[3]), ._5(_5_t_t), ._6(_6_t_t), ._7(a[6]), ._8(a[7]), .o(_7[13]));
  _1bit_8xAND _1bit_8xand_207 (
    ._1(_1_t_t), ._2(a[1]), ._3(a[2]), ._4(a[3]), ._5(_5_t_t), ._6(_6_t_t), ._7(a[6]), ._8(a[7]), .o(_7[14]));
  _1bit_8xAND _1bit_8xand_208 (
    ._1(a[0]), ._2(a[1]), ._3(a[2]), ._4(a[3]), ._5(_5_t_t), ._6(_6_t_t), ._7(a[6]), ._8(a[7]), .o(_7[15]));
  _1bit_8xAND _1bit_8xand_209 (
    ._1(_1_t_t), ._2(_2_t_t), ._3(_3_t_t), ._4(_4_t_t), ._5(a[4]), ._6(_6_t_t), ._7(a[6]), ._8(a[7]),
    .o(_7[16]));
  _1bit_8xAND _1bit_8xand_210 (
    ._1(a[0]), ._2(_2_t_t), ._3(_3_t_t), ._4(_4_t_t), ._5(a[4]), ._6(_6_t_t), ._7(a[6]), ._8(a[7]), .o(_7[17]));
  _1bit_8xAND _1bit_8xand_211 (
    ._1(_1_t_t), ._2(a[1]), ._3(_3_t_t), ._4(_4_t_t), ._5(a[4]), ._6(_6_t_t), ._7(a[6]), ._8(a[7]), .o(_7[18]));
  _1bit_8xAND _1bit_8xand_212 (
    ._1(a[0]), ._2(a[1]), ._3(_3_t_t), ._4(_4_t_t), ._5(a[4]), ._6(_6_t_t), ._7(a[6]), ._8(a[7]), .o(_7[19]));
  _1bit_8xAND _1bit_8xand_213 (
    ._1(_1_t_t), ._2(_2_t_t), ._3(a[2]), ._4(_4_t_t), ._5(a[4]), ._6(_6_t_t), ._7(a[6]), ._8(a[7]), .o(_7[20]));
  _1bit_8xAND _1bit_8xand_214 (
    ._1(a[0]), ._2(_2_t_t), ._3(a[2]), ._4(_4_t_t), ._5(a[4]), ._6(_6_t_t), ._7(a[6]), ._8(a[7]), .o(_7[21]));
  _1bit_8xAND _1bit_8xand_215 (
    ._1(_1_t_t), ._2(a[1]), ._3(a[2]), ._4(_4_t_t), ._5(a[4]), ._6(_6_t_t), ._7(a[6]), ._8(a[7]), .o(_7[22]));
  _1bit_8xAND _1bit_8xand_216 (
    ._1(a[0]), ._2(a[1]), ._3(a[2]), ._4(_4_t_t), ._5(a[4]), ._6(_6_t_t), ._7(a[6]), ._8(a[7]), .o(_7[23]));
  _1bit_8xAND _1bit_8xand_217 (
    ._1(_1_t_t), ._2(_2_t_t), ._3(_3_t_t), ._4(a[3]), ._5(a[4]), ._6(_6_t_t), ._7(a[6]), ._8(a[7]), .o(_7[24]));
  _1bit_8xAND _1bit_8xand_218 (
    ._1(a[0]), ._2(_2_t_t), ._3(_3_t_t), ._4(a[3]), ._5(a[4]), ._6(_6_t_t), ._7(a[6]), ._8(a[7]), .o(_7[25]));
  _1bit_8xAND _1bit_8xand_219 (
    ._1(_1_t_t), ._2(a[1]), ._3(_3_t_t), ._4(a[3]), ._5(a[4]), ._6(_6_t_t), ._7(a[6]), ._8(a[7]), .o(_7[26]));
  _1bit_8xAND _1bit_8xand_220 (
    ._1(a[0]), ._2(a[1]), ._3(_3_t_t), ._4(a[3]), ._5(a[4]), ._6(_6_t_t), ._7(a[6]), ._8(a[7]), .o(_7[27]));
  _1bit_8xAND _1bit_8xand_221 (
    ._1(_1_t_t), ._2(_2_t_t), ._3(a[2]), ._4(a[3]), ._5(a[4]), ._6(_6_t_t), ._7(a[6]), ._8(a[7]), .o(_7[28]));
  _1bit_8xAND _1bit_8xand_222 (
    ._1(a[0]), ._2(_2_t_t), ._3(a[2]), ._4(a[3]), ._5(a[4]), ._6(_6_t_t), ._7(a[6]), ._8(a[7]), .o(_7[29]));
  _1bit_8xAND _1bit_8xand_223 (
    ._1(_1_t_t), ._2(a[1]), ._3(a[2]), ._4(a[3]), ._5(a[4]), ._6(_6_t_t), ._7(a[6]), ._8(a[7]), .o(_7[30]));
  _1bit_8xAND _1bit_8xand_224 (
    ._1(a[0]), ._2(a[1]), ._3(a[2]), ._4(a[3]), ._5(a[4]), ._6(_6_t_t), ._7(a[6]), ._8(a[7]), .o(_7[31]));
  _1bit_8xAND _1bit_8xand_225 (
    ._1(_1_t_t), ._2(_2_t_t), ._3(_3_t_t), ._4(_4_t_t), ._5(_5_t_t), ._6(a[5]), ._7(a[6]), ._8(a[7]),
    .o(_8[0]));
  _1bit_8xAND _1bit_8xand_226 (
    ._1(a[0]), ._2(_2_t_t), ._3(_3_t_t), ._4(_4_t_t), ._5(_5_t_t), ._6(a[5]), ._7(a[6]), ._8(a[7]), .o(_8[1]));
  _1bit_8xAND _1bit_8xand_227 (
    ._1(_1_t_t), ._2(a[1]), ._3(_3_t_t), ._4(_4_t_t), ._5(_5_t_t), ._6(a[5]), ._7(a[6]), ._8(a[7]), .o(_8[2]));
  _1bit_8xAND _1bit_8xand_228 (
    ._1(a[0]), ._2(a[1]), ._3(_3_t_t), ._4(_4_t_t), ._5(_5_t_t), ._6(a[5]), ._7(a[6]), ._8(a[7]), .o(_8[3]));
  _1bit_8xAND _1bit_8xand_229 (
    ._1(_1_t_t), ._2(_2_t_t), ._3(a[2]), ._4(_4_t_t), ._5(_5_t_t), ._6(a[5]), ._7(a[6]), ._8(a[7]), .o(_8[4]));
  _1bit_8xAND _1bit_8xand_230 (
    ._1(a[0]), ._2(_2_t_t), ._3(a[2]), ._4(_4_t_t), ._5(_5_t_t), ._6(a[5]), ._7(a[6]), ._8(a[7]), .o(_8[5]));
  _1bit_8xAND _1bit_8xand_231 (
    ._1(_1_t_t), ._2(a[1]), ._3(a[2]), ._4(_4_t_t), ._5(_5_t_t), ._6(a[5]), ._7(a[6]), ._8(a[7]), .o(_8[6]));
  _1bit_8xAND _1bit_8xand_232 (
    ._1(a[0]), ._2(a[1]), ._3(a[2]), ._4(_4_t_t), ._5(_5_t_t), ._6(a[5]), ._7(a[6]), ._8(a[7]), .o(_8[7]));
  _1bit_8xAND _1bit_8xand_233 (
    ._1(_1_t_t), ._2(_2_t_t), ._3(_3_t_t), ._4(a[3]), ._5(_5_t_t), ._6(a[5]), ._7(a[6]), ._8(a[7]), .o(_8[8]));
  _1bit_8xAND _1bit_8xand_234 (
    ._1(a[0]), ._2(_2_t_t), ._3(_3_t_t), ._4(a[3]), ._5(_5_t_t), ._6(a[5]), ._7(a[6]), ._8(a[7]), .o(_8[9]));
  _1bit_8xAND _1bit_8xand_235 (
    ._1(_1_t_t), ._2(a[1]), ._3(_3_t_t), ._4(a[3]), ._5(_5_t_t), ._6(a[5]), ._7(a[6]), ._8(a[7]), .o(_8[10]));
  _1bit_8xAND _1bit_8xand_236 (
    ._1(a[0]), ._2(a[1]), ._3(_3_t_t), ._4(a[3]), ._5(_5_t_t), ._6(a[5]), ._7(a[6]), ._8(a[7]), .o(_8[11]));
  _1bit_8xAND _1bit_8xand_237 (
    ._1(_1_t_t), ._2(_2_t_t), ._3(a[2]), ._4(a[3]), ._5(_5_t_t), ._6(a[5]), ._7(a[6]), ._8(a[7]), .o(_8[12]));
  _1bit_8xAND _1bit_8xand_238 (
    ._1(a[0]), ._2(_2_t_t), ._3(a[2]), ._4(a[3]), ._5(_5_t_t), ._6(a[5]), ._7(a[6]), ._8(a[7]), .o(_8[13]));
  _1bit_8xAND _1bit_8xand_239 (
    ._1(_1_t_t), ._2(a[1]), ._3(a[2]), ._4(a[3]), ._5(_5_t_t), ._6(a[5]), ._7(a[6]), ._8(a[7]), .o(_8[14]));
  _1bit_8xAND _1bit_8xand_240 (
    ._1(a[0]), ._2(a[1]), ._3(a[2]), ._4(a[3]), ._5(_5_t_t), ._6(a[5]), ._7(a[6]), ._8(a[7]), .o(_8[15]));
  _1bit_8xAND _1bit_8xand_241 (
    ._1(_1_t_t), ._2(_2_t_t), ._3(_3_t_t), ._4(_4_t_t), ._5(a[4]), ._6(a[5]), ._7(a[6]), ._8(a[7]), .o(_8[16]));
  _1bit_8xAND _1bit_8xand_242 (
    ._1(a[0]), ._2(_2_t_t), ._3(_3_t_t), ._4(_4_t_t), ._5(a[4]), ._6(a[5]), ._7(a[6]), ._8(a[7]), .o(_8[17]));
  _1bit_8xAND _1bit_8xand_243 (
    ._1(_1_t_t), ._2(a[1]), ._3(_3_t_t), ._4(_4_t_t), ._5(a[4]), ._6(a[5]), ._7(a[6]), ._8(a[7]), .o(_8[18]));
  _1bit_8xAND _1bit_8xand_244 (
    ._1(a[0]), ._2(a[1]), ._3(_3_t_t), ._4(_4_t_t), ._5(a[4]), ._6(a[5]), ._7(a[6]), ._8(a[7]), .o(_8[19]));
  _1bit_8xAND _1bit_8xand_245 (
    ._1(_1_t_t), ._2(_2_t_t), ._3(a[2]), ._4(_4_t_t), ._5(a[4]), ._6(a[5]), ._7(a[6]), ._8(a[7]), .o(_8[20]));
  _1bit_8xAND _1bit_8xand_246 (
    ._1(a[0]), ._2(_2_t_t), ._3(a[2]), ._4(_4_t_t), ._5(a[4]), ._6(a[5]), ._7(a[6]), ._8(a[7]), .o(_8[21]));
  _1bit_8xAND _1bit_8xand_247 (
    ._1(_1_t_t), ._2(a[1]), ._3(a[2]), ._4(_4_t_t), ._5(a[4]), ._6(a[5]), ._7(a[6]), ._8(a[7]), .o(_8[22]));
  _1bit_8xAND _1bit_8xand_248 (
    ._1(a[0]), ._2(a[1]), ._3(a[2]), ._4(_4_t_t), ._5(a[4]), ._6(a[5]), ._7(a[6]), ._8(a[7]), .o(_8[23]));
  _1bit_8xAND _1bit_8xand_249 (
    ._1(_1_t_t), ._2(_2_t_t), ._3(_3_t_t), ._4(a[3]), ._5(a[4]), ._6(a[5]), ._7(a[6]), ._8(a[7]), .o(_8[24]));
  _1bit_8xAND _1bit_8xand_250 (
    ._1(a[0]), ._2(_2_t_t), ._3(_3_t_t), ._4(a[3]), ._5(a[4]), ._6(a[5]), ._7(a[6]), ._8(a[7]), .o(_8[25]));
  _1bit_8xAND _1bit_8xand_251 (
    ._1(_1_t_t), ._2(a[1]), ._3(_3_t_t), ._4(a[3]), ._5(a[4]), ._6(a[5]), ._7(a[6]), ._8(a[7]), .o(_8[26]));
  _1bit_8xAND _1bit_8xand_252 (
    ._1(a[0]), ._2(a[1]), ._3(_3_t_t), ._4(a[3]), ._5(a[4]), ._6(a[5]), ._7(a[6]), ._8(a[7]), .o(_8[27]));
  _1bit_8xAND _1bit_8xand_253 (
    ._1(_1_t_t), ._2(_2_t_t), ._3(a[2]), ._4(a[3]), ._5(a[4]), ._6(a[5]), ._7(a[6]), ._8(a[7]), .o(_8[28]));
  _1bit_8xAND _1bit_8xand_254 (
    ._1(a[0]), ._2(_2_t_t), ._3(a[2]), ._4(a[3]), ._5(a[4]), ._6(a[5]), ._7(a[6]), ._8(a[7]), .o(_8[29]));
  _1bit_8xAND _1bit_8xand_255 (
    ._1(_1_t_t), ._2(a[1]), ._3(a[2]), ._4(a[3]), ._5(a[4]), ._6(a[5]), ._7(a[6]), ._8(a[7]), .o(_8[30]));
  _1bit_8xAND _1bit_8xand_256 (
    ._1(a[0]), ._2(a[1]), ._3(a[2]), ._4(a[3]), ._5(a[4]), ._6(a[5]), ._7(a[6]), ._8(a[7]), .o(_8[31]));

  // Other names for the same wires on the sheet: _1_t = a[0]; _2_t = a[1]; _3_t = a[2]; _4_t = a[3]; _5_t = a[4];
  //   _6_t = a[5]; _7_t = a[6]; _8_t = a[7]
endmodule
