// Digital circuit 8bit_Register.dig as structural Verilog
module _8bit_Register (
  input  gt_C,
  input  [7:0] D,
  input  enb_w,
  output [7:0] Q
);

  _1bit_Register _1bit_register_1 (.D(D[0]), .gt_C(gt_C), .enb(enb_w), .Q(Q[0]));
  _1bit_Register _1bit_register_2 (.D(D[1]), .gt_C(gt_C), .enb(enb_w), .Q(Q[1]));
  _1bit_Register _1bit_register_3 (.D(D[2]), .gt_C(gt_C), .enb(enb_w), .Q(Q[2]));
  _1bit_Register _1bit_register_4 (.D(D[3]), .gt_C(gt_C), .enb(enb_w), .Q(Q[3]));
  _1bit_Register _1bit_register_5 (.D(D[4]), .gt_C(gt_C), .enb(enb_w), .Q(Q[4]));
  _1bit_Register _1bit_register_6 (.D(D[5]), .gt_C(gt_C), .enb(enb_w), .Q(Q[5]));
  _1bit_Register _1bit_register_7 (.D(D[6]), .gt_C(gt_C), .enb(enb_w), .Q(Q[6]));
  _1bit_Register _1bit_register_8 (.D(D[7]), .gt_C(gt_C), .enb(enb_w), .Q(Q[7]));
endmodule
