// Digital circuit 8bit_Router.dig as structural Verilog
module _8bit_Router (
  input  [7:0] val,
  input  sel,
  input  enb,
  output [7:0] a,
  output [7:0] b
);

  wire and_1_out, and_2_out, not_1_out;

  not not_1 (not_1_out, sel);
  and and_1 (and_1_out, sel, enb);
  and and_2 (and_2_out, enb, not_1_out);
  assign a = and_2_out ? val : 8'bz;  // Driver driver_1
  assign b = and_1_out ? val : 8'bz;  // Driver driver_2
endmodule
