// Digital circuit ALU.dig as structural Verilog
module ALU (
  input  [3:0] op,
  input  [31:0] a,
  input  [31:0] b,
  input  [4:0] shamt,
  output [31:0] o,
  output zero,
  output SLT,
  output USLT
);

  wire _32bit_eq_1_o, _32bit_sub_1_c_out, _32bit_sub_1_of, xor_2_out;
  wire [31:0] _32bit_adder_1_s, _32bit_sll_1_o, _32bit_sra_1_o, _32bit_srl_1_o, _32bit_sub_1_s, and_1_out,
       or_1_out, xor_1_out;

  _32bit_Adder _32bit_adder_1 (.a(a), .b(b), .s(_32bit_adder_1_s));  // open: c_out
  _32bit_Sub _32bit_sub_1 (.a(a), .b(b), .s(_32bit_sub_1_s), .c_out(_32bit_sub_1_c_out), .of(_32bit_sub_1_of));
  assign and_1_out = a & b;  // And and_1, 32 bits wide
  assign or_1_out = a | b;  // Or or_1, 32 bits wide
  assign xor_1_out = a ^ b;  // XOr xor_1, 32 bits wide
  _32bit_SLL _32bit_sll_1 (.shamt(shamt), .i(a), .o(_32bit_sll_1_o));
  _32bit_SRL _32bit_srl_1 (.shamt(shamt), .i(a), .o(_32bit_srl_1_o));
  _32bit_SRA _32bit_sra_1 (.shamt(shamt), .i(a), .o(_32bit_sra_1_o));
  xor xor_2 (xor_2_out, _32bit_sub_1_s[31], _32bit_sub_1_of);
  not not_1 (SLT, xor_2_out);
  not not_2 (USLT, _32bit_sub_1_c_out);
  _32bit_EQ _32bit_eq_1 (.a({32{1'b0}}), .b(_32bit_sub_1_s), .o(_32bit_eq_1_o));
  Multiplexer #(.Selector_Bits(4), .Bits(32)) multiplexer_1 (
    .sel(op), .in_0(_32bit_adder_1_s), .in_1(_32bit_sub_1_s), .in_2(and_1_out), .in_3(or_1_out),
    .in_4(xor_1_out), .in_5(_32bit_sll_1_o), .in_6(_32bit_srl_1_o), .in_7(_32bit_sra_1_o), .in_8({32{1'b0}}),
    .in_9({32{1'b0}}), .in_10({32{1'b0}}), .in_11({32{1'b0}}), .in_12({32{1'b0}}), .in_13({32{1'b0}}),
    .in_14({32{1'b0}}), .in_15({32{1'b0}}), .out(o));
  not not_3 (zero, _32bit_eq_1_o);
endmodule
