// Digital circuit Clock.dig as structural Verilog
module Clock (
  input  enb,
  input  rst,
  input  CLK_in,
  output PC_r,
  output gt_C
);

  wire not_1_out, reset_1_out;

  Reset #(.invertOutput("false")) reset_1 (.out(reset_1_out));
  xor xor_1 (PC_r, reset_1_out, rst);
  not not_1 (not_1_out, reset_1_out);
  and and_1 (gt_C, CLK_in, enb, not_1_out);
endmodule
