// Digital circuit Comparator.dig as structural Verilog
module Comparator (
  input  [31:0] a,
  input  [31:0] b,
  output Zero,
  output SLT,
  output SLTU
);

  wire _32bit_eq_1_o, _32bit_sub_1_c_out, _32bit_sub_1_of;
  wire [31:0] _32bit_sub_1_s;

  _32bit_Sub _32bit_sub_1 (.a(a), .b(b), .s(_32bit_sub_1_s), .c_out(_32bit_sub_1_c_out), .of(_32bit_sub_1_of));
  _32bit_EQ _32bit_eq_1 (.a({32{1'b0}}), .b(_32bit_sub_1_s), .o(_32bit_eq_1_o));
  xnor xnor_1 (SLT, _32bit_sub_1_s[31], _32bit_sub_1_of);
  not not_1 (SLTU, _32bit_sub_1_c_out);
  not not_2 (Zero, _32bit_eq_1_o);
endmodule
