// Digital circuit Instruction_Decoder.dig as structural Verilog
module Instruction_Decoder (
  input  [31:0] instr,
  output RegWrite,
  output [1:0] RegSrc,
  output ALUSrc,
  output [2:0] ALUCtrl,
  output [2:0] ImmSel,
  output MemRead,
  output MemWrite,
  output [3:0] MemMask,
  output MemUnsigned,
  output [2:0] BranchType,
  output Jump,
  output JumpReg,
  output ALUSrcA,
  output PCSrc
);

  wire and_1_out, and_2_out, and_5_out, and_6_out, and_8_out, and_9_out, and_10_out, and_11_out, and_12_out,
       and_13_out, decoder_1_out_0, decoder_1_out_1, decoder_1_out_4, decoder_1_out_5, decoder_1_out_6,
       decoder_1_out_7, decoder_2_out_0, decoder_2_out_1, decoder_3_out_0, decoder_3_out_1, decoder_3_out_4,
       decoder_3_out_5, or_1_out;
  wire [2:0] pulldown_1_out;

  and and_1 (and_1_out, instr[0], instr[1], ~instr[2], ~instr[3], instr[4], instr[5], ~instr[6]);  // And
  and and_2 (and_2_out, instr[0], instr[1], ~instr[2], ~instr[3], instr[4], ~instr[5], ~instr[6]);  // And
  and and_3 (MemRead, instr[0], instr[1], ~instr[2], ~instr[3], ~instr[4], ~instr[5], ~instr[6]);  // And
  and and_4 (MemWrite, instr[0], instr[1], ~instr[2], ~instr[3], ~instr[4], instr[5], ~instr[6]);  // And
  and and_5 (and_5_out, instr[0], instr[1], ~instr[2], ~instr[3], ~instr[4], instr[5], instr[6]);  // And
  and and_6 (and_6_out, instr[0], instr[1], instr[2], instr[3], ~instr[4], instr[5], instr[6]);  // And
  and and_7 (JumpReg, instr[0], instr[1], instr[2], ~instr[3], ~instr[4], instr[5], instr[6]);  // And
  and and_8 (and_8_out, instr[0], instr[1], instr[2], ~instr[3], instr[4], instr[5], ~instr[6]);  // And
  and and_9 (and_9_out, instr[0], instr[1], instr[2], ~instr[3], instr[4], ~instr[5], ~instr[6]);  // And
  or or_1 (or_1_out, and_2_out, and_1_out);
  PullDown #(.Bits(3)) pulldown_1 (.out(pulldown_1_out));
  Decoder #(.Selector_Bits(3)) decoder_1 (
    .sel(pulldown_1_out), .out_0(decoder_1_out_0), .out_1(decoder_1_out_1), .out_4(decoder_1_out_4),
    .out_5(decoder_1_out_5), .out_6(decoder_1_out_6), .out_7(decoder_1_out_7));  // open: out_2, out_3
  Decoder decoder_2 (.sel(instr[26]), .out_0(decoder_2_out_0), .out_1(decoder_2_out_1));
  Decoder #(.Selector_Bits(3)) decoder_3 (
    .sel(instr[14:12]), .out_0(decoder_3_out_0), .out_1(decoder_3_out_1), .out_2(MemMask[3]),
    .out_4(decoder_3_out_4), .out_5(decoder_3_out_5));  // open: out_3, out_6, out_7
  assign pulldown_1_out = or_1_out ? instr[14:12] : 3'bz;  // Driver driver_1
  and and_10 (and_10_out, decoder_1_out_5, decoder_2_out_0);
  and and_11 (and_11_out, decoder_2_out_1, decoder_1_out_5);
  and and_12 (and_12_out, ~instr[25], ~instr[26], ~instr[27], ~instr[28], ~instr[29], instr[30], ~instr[31]);  // And
  or or_2 (RegWrite, JumpReg, and_1_out, and_2_out, and_6_out, and_9_out, MemRead, and_8_out);
  or or_3 (RegSrc[0], MemRead, and_8_out);
  or or_4 (RegSrc[1], and_6_out, JumpReg, and_8_out);
  or or_5 (ALUSrc, MemRead, and_2_out, and_9_out, MemWrite, JumpReg, and_6_out);
  or or_6 (Jump, JumpReg, and_6_out);
  or or_7 (ImmSel[0], and_2_out, MemRead, JumpReg, and_6_out, and_5_out);
  or or_8 (ImmSel[1], and_5_out, MemWrite);
  or or_9 (ImmSel[2], and_8_out, and_6_out, and_9_out);
  or or_10 (MemMask[0], decoder_3_out_0, decoder_3_out_1, MemMask[3], decoder_3_out_4, decoder_3_out_5);
  or or_11 (MemMask[1], decoder_3_out_1, decoder_3_out_5, MemMask[3]);
  or or_12 (MemUnsigned, decoder_3_out_5, decoder_3_out_4);
  or or_13 (ALUSrcA, and_6_out, JumpReg, and_9_out);
  or or_14 (PCSrc, and_6_out, JumpReg);
  and and_13 (and_13_out, and_12_out, decoder_1_out_0);
  or or_15 (ALUCtrl[0], and_13_out, and_5_out, decoder_1_out_1, and_11_out, decoder_1_out_6);
  or or_16 (ALUCtrl[1], decoder_1_out_6, and_11_out, decoder_1_out_7, and_10_out);
  or or_17 (ALUCtrl[2], decoder_1_out_4, decoder_1_out_1, and_11_out, and_10_out);

  assign BranchType = instr[14:12];
  assign MemMask[2] = MemMask[3];

  // Notes on the sheet:
  //   R-Type
  //   I-Type
  //   Load
  //   Store
  //   Branch
  //   JAL
  //   JALR
  //   LUI
  //   AUIPC
endmodule
