// Digital circuit PC.dig as structural Verilog
module PC (
  input  rst,
  input  gt_C,
  input  [31:0] def,
  input  [31:0] addr_in,
  output [31:0] o_cur
);

  wire or_1_out, reset_1_out;
  wire [31:0] _32bit_2xmux_1_o;

  Reset #(.invertOutput("false")) reset_1 (.out(reset_1_out));
  or or_1 (or_1_out, reset_1_out, rst);
  _32bit_2xMUX _32bit_2xmux_1 (.sel(or_1_out), .a(addr_in), .b(def), .o(_32bit_2xmux_1_o));
  _8bit_Register _8bit_register_1 (.gt_C(gt_C), .D(_32bit_2xmux_1_o[7:0]), .enb_w(1'b1), .Q(o_cur[7:0]));
  _8bit_Register _8bit_register_2 (.gt_C(gt_C), .D(_32bit_2xmux_1_o[15:8]), .enb_w(1'b1), .Q(o_cur[15:8]));
  _8bit_Register _8bit_register_3 (.gt_C(gt_C), .D(_32bit_2xmux_1_o[23:16]), .enb_w(1'b1), .Q(o_cur[23:16]));
  _8bit_Register _8bit_register_4 (.gt_C(gt_C), .D(_32bit_2xmux_1_o[31:24]), .enb_w(1'b1), .Q(o_cur[31:24]));
endmodule
