// Digital circuit PC_Adder.dig as structural Verilog
module PC_Adder (
  input  br_enb,
  input  [31:0] br_off,
  input  [31:0] o_addr,
  output [31:0] n_addr
);

  wire _8bit_adder_1_c_out, _8bit_adder_2_c_out, _8bit_adder_3_c_out;
  wire [7:0] _32bit_2xmux_1_o, _32bit_2xmux_1_o_2, _32bit_2xmux_1_o_3, _32bit_2xmux_1_o_4;

  _8bit_Adder _8bit_adder_1 (
    .a(o_addr[7:0]), .b(_32bit_2xmux_1_o), .c_in(1'b0), .s(n_addr[7:0]), .c_out(_8bit_adder_1_c_out));
  _8bit_Adder _8bit_adder_2 (
    .a(o_addr[15:8]), .b(_32bit_2xmux_1_o_2), .c_in(_8bit_adder_1_c_out), .s(n_addr[15:8]),
    .c_out(_8bit_adder_2_c_out));
  _8bit_Adder _8bit_adder_3 (
    .a(o_addr[23:16]), .b(_32bit_2xmux_1_o_3), .c_in(_8bit_adder_2_c_out), .s(n_addr[23:16]),
    .c_out(_8bit_adder_3_c_out));
  _8bit_Adder _8bit_adder_4 (
    .a(o_addr[31:24]), .b(_32bit_2xmux_1_o_4), .c_in(_8bit_adder_3_c_out), .s(n_addr[31:24]));  // open: c_out
  _32bit_2xMUX _32bit_2xmux_1 (
    .sel(br_enb), .a(32'h1), .b(br_off),
    .o({_32bit_2xmux_1_o_4, _32bit_2xmux_1_o_3, _32bit_2xmux_1_o_2, _32bit_2xmux_1_o}));
endmodule
