// Digital circuit PC_Control.dig as structural Verilog
module PC_Control (
  input  Branch,
  input  [2:0] BranchType,
  input  Jump,
  input  JumpReg,
  input  Zero,
  input  SLT,
  input  SLTU,
  output PCSrc
);

  wire and_1_out, and_2_out, and_3_out, and_4_out, and_5_out, and_6_out, and_7_out, decoder_1_out_0,
       decoder_1_out_1, decoder_1_out_4, decoder_1_out_5, decoder_1_out_6, decoder_1_out_7, or_1_out;

  Decoder #(.Selector_Bits(3)) decoder_1 (
    .sel(BranchType), .out_0(decoder_1_out_0), .out_1(decoder_1_out_1), .out_4(decoder_1_out_4),
    .out_5(decoder_1_out_5), .out_6(decoder_1_out_6), .out_7(decoder_1_out_7));  // open: out_2, out_3
  and and_1 (and_1_out, Zero, decoder_1_out_0);
  and and_2 (and_2_out, decoder_1_out_1, ~Zero);  // And
  and and_3 (and_3_out, SLT, decoder_1_out_4);
  and and_4 (and_4_out, decoder_1_out_5, ~SLT);  // And
  and and_5 (and_5_out, SLTU, decoder_1_out_6);
  and and_6 (and_6_out, decoder_1_out_7, ~SLTU);  // And
  or or_1 (or_1_out, and_1_out, and_2_out, and_3_out, and_4_out, and_5_out, and_6_out);
  and and_7 (and_7_out, Branch, or_1_out);
  or or_2 (PCSrc, and_7_out, Jump, JumpReg);
endmodule
