// Digital circuit RAM_Cell.dig as structural Verilog
module RAM_Cell (
  input  w_enb,
  input  [3:0] w_mask,
  input  r_enb,
  input  [31:0] D,
  input  gt_C,
  output [31:0] Q
);

  wire and_1_out, and_2_out, and_3_out, and_4_out;
  wire [7:0] _8bit_register_1_q, _8bit_register_2_q, _8bit_register_3_q, _8bit_register_4_q;

  and and_1 (and_1_out, w_enb, w_mask[0]);
  and and_2 (and_2_out, w_enb, w_mask[1]);
  and and_3 (and_3_out, w_enb, w_mask[2]);
  and and_4 (and_4_out, w_enb, w_mask[3]);
  _8bit_Register _8bit_register_1 (.gt_C(gt_C), .D(D[7:0]), .enb_w(and_1_out), .Q(_8bit_register_1_q));
  _8bit_Register _8bit_register_2 (.gt_C(gt_C), .D(D[15:8]), .enb_w(and_2_out), .Q(_8bit_register_2_q));
  _8bit_Register _8bit_register_3 (.gt_C(gt_C), .D(D[23:16]), .enb_w(and_3_out), .Q(_8bit_register_3_q));
  _8bit_Register _8bit_register_4 (.gt_C(gt_C), .D(D[31:24]), .enb_w(and_4_out), .Q(_8bit_register_4_q));
  assign Q = r_enb ? {_8bit_register_4_q, _8bit_register_3_q, _8bit_register_2_q, _8bit_register_1_q} : 32'bz;  // Driver driver_1
endmodule
