// Digital circuit RE_D_Latch.dig as structural Verilog
module RE_D_Latch (
  input  D,
  input  gt_C,
  output Q,
  output Q_2
);

  wire nand_1_out, nand_2_out, not_1_out, not_2_out, or_1_out, pulse_generator_1_o, reset_1_out;

  pulse_generator pulse_generator_1 (.i(gt_C), .o(pulse_generator_1_o));
  Reset reset_1 (.out(reset_1_out));
  not not_1 (not_1_out, reset_1_out);
  or or_1 (or_1_out, pulse_generator_1_o, not_1_out);
  not not_2 (not_2_out, D);
  nand nand_1 (nand_1_out, D, or_1_out);
  nand nand_2 (nand_2_out, or_1_out, not_2_out);
  nand nand_3 (Q, nand_1_out, Q_2);
  nand nand_4 (Q_2, Q, nand_2_out);
endmodule
