// Digital circuit ROM.dig as structural Verilog
module ROM (
  input  [31:0] D,
  input  gt_C,
  input  [31:0] addr_r1,
  output [31:0] Q_1,
  output [31:0] Q_2
);

  wire ram_cell_1_p2, ram_cell_2_p2, ram_cell_3_p2, ram_cell_4_p2, ram_cell_5_p2, ram_cell_6_p2,
       ram_cell_7_p2, ram_cell_7_p6, ram_cell_7_p7;
  wire [31:0] _8bit_decoder_1__1, _8bit_decoder_1__2, _8bit_decoder_1__3, _8bit_decoder_1__4,
       _8bit_decoder_1__5, _8bit_decoder_1__6, _8bit_decoder_1__7, _8bit_decoder_1__8,
       _32bit_signal_extend_1_o, _256bit_and_1_o_1, _256bit_and_1_o_2, _256bit_and_1_o_3, _256bit_and_1_o_4,
       _256bit_and_1_o_5, _256bit_and_1_o_6, _256bit_and_1_o_7, _256bit_and_1_o_8;

  _32bit_signal_extend _32bit_signal_extend_1 (.i(1'b1), .o(_32bit_signal_extend_1_o));
  _8bit_Decoder _8bit_decoder_1 (
    .a(addr_r1[9:2]), ._1(_8bit_decoder_1__1), ._2(_8bit_decoder_1__2), ._3(_8bit_decoder_1__3),
    ._4(_8bit_decoder_1__4), ._5(_8bit_decoder_1__5), ._6(_8bit_decoder_1__6), ._7(_8bit_decoder_1__7),
    ._8(_8bit_decoder_1__8));
  _256bit_AND _256bit_and_1 (
    .i_1(_8bit_decoder_1__1), .i_2(_8bit_decoder_1__2), .i_3(_8bit_decoder_1__3), .i_4(_8bit_decoder_1__4),
    .i_5(_8bit_decoder_1__5), .i_6(_8bit_decoder_1__6), .i_7(_8bit_decoder_1__7), .i_8(_8bit_decoder_1__8),
    .enb(_32bit_signal_extend_1_o), .o_1(_256bit_and_1_o_1), .o_2(_256bit_and_1_o_2),
    .o_3(_256bit_and_1_o_3), .o_4(_256bit_and_1_o_4), .o_5(_256bit_and_1_o_5), .o_6(_256bit_and_1_o_6),
    .o_7(_256bit_and_1_o_7), .o_8(_256bit_and_1_o_8));
  _256bit_AND _256bit_and_2 ();  // open: i_1, i_2, i_3, i_4, i_5, i_6, i_7, i_8, enb, o_1, o_2, o_3, o_4, o_5, o_6, o_7, o_8
  // RAM_Cell ram_cell_1: pin names not known; wires that end beside it: addr_r1[1:0], ram_cell_1_p2, D, gt_C, Q_1
  // RAM_Cell ram_cell_2: pin names not known; wires that end beside it: addr_r1[1:0], ram_cell_2_p2, D, gt_C, Q_1
  // RAM_Cell ram_cell_3: pin names not known; wires that end beside it: addr_r1[1:0], ram_cell_3_p2, D, gt_C, Q_1
  // RAM_Cell ram_cell_4: pin names not known; wires that end beside it: addr_r1[1:0], ram_cell_4_p2, D, gt_C, Q_1
  // RAM_Cell ram_cell_5: pin names not known; wires that end beside it: addr_r1[1:0], ram_cell_5_p2, D, gt_C, Q_1
  // RAM_Cell ram_cell_6: pin names not known; wires that end beside it: addr_r1[1:0], ram_cell_6_p2, D, gt_C, Q_1
  // RAM_Cell ram_cell_7: pin names not known; wires that end beside it: addr_r1[1:0], ram_cell_7_p2, D, gt_C, Q_1, ram_cell_7_p6, ram_cell_7_p7
  // RAM_Cell ram_cell_8: pin names not known; wires that end beside it: addr_r1[1:0], ram_cell_7_p7, D, gt_C, Q_1

  // Other names for the same wires on the sheet: r1_addr[1:0] = addr_r1[1:0]

  // Notes on the sheet:
  //   D: Data input
  //   gt_C: Clock input
  //   Q_1: Output of register 1
  //   addr_r1: Address of first register to read from
  //   Q_2: Output of register 2
endmodule
