// Digital circuit RV321_CPU.dig as structural Verilog
module RV321_CPU (
  input  PC_reset,
  input  gt_C_enb,
  input  CLK
);

  wire CLC_step_out, clock_1_gt_c, clock_1_pc_r, comparator_1_slt, comparator_1_sltu, comparator_1_zero,
       instruction_decoder_1_alusrc, instruction_decoder_1_alusrca, instruction_decoder_1_branch,
       instruction_decoder_1_jump, instruction_decoder_1_jumpreg, instruction_decoder_1_memread,
       instruction_decoder_1_memwrite, instruction_decoder_1_regwrite, or_1_out, pc_control_1_pcsrc,
       reset_1_out;
  wire [1:0] instruction_decoder_1_regsrc;
  wire [2:0] instruction_decoder_1_aluctrl, instruction_decoder_1_branchtype, instruction_decoder_1_immsel;
  wire [3:0] instruction_decoder_1_memmask;
  wire [4:0] multiplexer_2_out_2, multiplexer_2_out_3;
  wire [31:0] alu_1_o, immediate_generator_1_imm, multiplexer_1_out, multiplexer_2_out, multiplexer_3_out,
       multiplexer_4_out, multiplexer_5_out, pc_1_o_cur, pc_adder_1_n_addr, PROG_d, ram_1_q,
       register_file_1_rs1, register_file_1_rs2;

  Clock clock_1 (.enb(gt_C_enb), .rst(PC_reset), .CLK_in(CLK), .PC_r(clock_1_pc_r), .gt_C(clock_1_gt_c));
  Button CLC_step (.out(CLC_step_out));
  or or_1 (or_1_out, clock_1_gt_c, CLC_step_out);
  Multiplexer #(.Bits(32)) multiplexer_1 (
    .sel(pc_control_1_pcsrc), .in_0(pc_adder_1_n_addr), .in_1(alu_1_o), .out(multiplexer_1_out));
  // Probe on pc_1_o_cur
  PC pc_1 (.rst(clock_1_pc_r), .gt_C(or_1_out), .def({32{1'b0}}), .addr_in(multiplexer_1_out), .o_cur(pc_1_o_cur));
  // Probe on {multiplexer_2_out[31:25], multiplexer_2_out_3, multiplexer_2_out_2, multiplexer_2_out[14:0]}
  ROM #(.bigEndian("true"), .AddrBits(24), .isProgramMemory("true"), .Bits(32)) PROG (
    .A(pc_1_o_cur[23:0]), .sel(1'b1), .D(PROG_d));
  PC_Adder pc_adder_1 (.incr(32'h4), .o_addr(pc_1_o_cur), .n_addr(pc_adder_1_n_addr));
  Multiplexer #(.Bits(32)) multiplexer_2 (
    .sel(reset_1_out), .in_0({32{1'b0}}), .in_1(PROG_d),
    .out({multiplexer_2_out[31:25], multiplexer_2_out_3, multiplexer_2_out_2, multiplexer_2_out[14:0]}));
  Instruction_Decoder instruction_decoder_1 (
    .instr({multiplexer_2_out[31:25], multiplexer_2_out_3, multiplexer_2_out_2, multiplexer_2_out[14:0]}),
    .RegWrite(instruction_decoder_1_regwrite), .RegSrc(instruction_decoder_1_regsrc),
    .ALUSrc(instruction_decoder_1_alusrc), .ALUCtrl(instruction_decoder_1_aluctrl),
    .ImmSel(instruction_decoder_1_immsel), .MemRead(instruction_decoder_1_memread),
    .MemWrite(instruction_decoder_1_memwrite), .MemMask(instruction_decoder_1_memmask),
    .BranchType(instruction_decoder_1_branchtype), .Jump(instruction_decoder_1_jump),
    .JumpReg(instruction_decoder_1_jumpreg), .ALUSrcA(instruction_decoder_1_alusrca),
    .Branch(instruction_decoder_1_branch));  // open: MemUnsigned
  Reset reset_1 (.out(reset_1_out));
  PC_Control pc_control_1 (
    .Branch(instruction_decoder_1_branch), .BranchType(instruction_decoder_1_branchtype),
    .Jump(instruction_decoder_1_jump), .JumpReg(instruction_decoder_1_jumpreg), .Zero(comparator_1_zero),
    .SLT(comparator_1_slt), .SLTU(comparator_1_sltu), .PCSrc(pc_control_1_pcsrc));
  Multiplexer #(.Selector_Bits(2), .Bits(32)) multiplexer_3 (
    .sel(instruction_decoder_1_regsrc), .in_0(alu_1_o), .in_1(ram_1_q), .in_2(pc_adder_1_n_addr),
    .in_3(immediate_generator_1_imm), .out(multiplexer_3_out));
  Immediate_Generator immediate_generator_1 (
    .instr({multiplexer_2_out[31:25], multiplexer_2_out_3, multiplexer_2_out_2, multiplexer_2_out[14:0]}),
    .\type (instruction_decoder_1_immsel), .imm(immediate_generator_1_imm));
  Comparator comparator_1 (
    .a(register_file_1_rs1), .b(register_file_1_rs2), .Zero(comparator_1_zero), .SLT(comparator_1_slt),
    .SLTU(comparator_1_sltu));
  Register_File register_file_1 (
    .D(multiplexer_3_out), .gt_C(or_1_out), .rs1_addr(multiplexer_2_out_2), .rs2_addr(multiplexer_2_out_3),
    .rd_addr(multiplexer_2_out[11:7]), .r_enb(1'b1), .w_enb(instruction_decoder_1_regwrite),
    .rs1(register_file_1_rs1), .rs2(register_file_1_rs2));
  Multiplexer #(.Bits(32)) multiplexer_4 (
    .sel(instruction_decoder_1_alusrca), .in_0(register_file_1_rs1), .in_1(pc_1_o_cur),
    .out(multiplexer_4_out));
  Multiplexer #(.Bits(32)) multiplexer_5 (
    .sel(instruction_decoder_1_alusrc), .in_0(register_file_1_rs2), .in_1(immediate_generator_1_imm),
    .out(multiplexer_5_out));
  ALU alu_1 (
    .op(instruction_decoder_1_aluctrl), .a(multiplexer_4_out), .b(multiplexer_5_out),
    .shamt(multiplexer_2_out_3), .o(alu_1_o));
  RAM ram_1 (
    .D(register_file_1_rs2), .gt_C(or_1_out), .w_mask(instruction_decoder_1_memmask), .r_addr(alu_1_o),
    .w_addr(alu_1_o), .r_enb(instruction_decoder_1_memread), .w_enb(instruction_decoder_1_memwrite),
    .Q(ram_1_q));

  // Notes on the sheet:
  //   contents of PROG (hex, n*v repeats v):
  //   26*0,4
endmodule
