// Digital circuit Register_File.dig as structural Verilog
module Register_File (
  input  [31:0] D,
  input  gt_C,
  input  [4:0] rs1_addr,
  input  [4:0] rs2_addr,
  input  [4:0] rd_addr,
  input  r_enb,
  input  w_enb,
  output [31:0] rs1,
  output [31:0] rs2
);

  wire [7:0] and_3_out_2;
  wire [23:0] and_3_out;
  wire [31:0] _5bit_mux_1_o, _5bit_mux_2_o, _5bit_mux_3_o, _32bit_signal_extend_1_o,
       _32bit_signal_extend_2_o, and_1_out, and_2_out;

  _32bit_signal_extend _32bit_signal_extend_1 (.i(w_enb), .o(_32bit_signal_extend_1_o));
  _5bit_MUX _5bit_mux_1 (.a(rd_addr), .o(_5bit_mux_1_o));
  _32bit_signal_extend _32bit_signal_extend_2 (.i(r_enb), .o(_32bit_signal_extend_2_o));
  _5bit_MUX _5bit_mux_2 (.a(rs2_addr), .o(_5bit_mux_2_o));
  assign and_1_out = _32bit_signal_extend_1_o & _5bit_mux_1_o;  // And and_1, 32 bits wide
  _5bit_MUX _5bit_mux_3 (.a(rs1_addr), .o(_5bit_mux_3_o));
  assign and_2_out = _32bit_signal_extend_2_o & _5bit_mux_2_o;  // And and_2, 32 bits wide
  assign {and_3_out_2, and_3_out} = _32bit_signal_extend_2_o & _5bit_mux_3_o;  // And and_3, 32 bits wide
  assign rs1 = and_3_out[0] ? {32{1'b0}} : 32'bz;  // Driver driver_1
  assign rs2 = and_2_out[0] ? {32{1'b0}} : 32'bz;  // Driver driver_2
  _32bit_Register _32bit_register_1 (
    .gt_C(gt_C), .D(D), .w_enb(and_1_out[8]), .rs1_enb(and_3_out[8]), .rs2_enb(and_2_out[8]), .rs1(rs1),
    .rs2(rs2));
  _32bit_Register _32bit_register_2 (
    .gt_C(gt_C), .D(D), .w_enb(and_1_out[1]), .rs1_enb(and_3_out[1]), .rs2_enb(and_2_out[1]), .rs1(rs1),
    .rs2(rs2));
  _32bit_Register _32bit_register_3 (
    .gt_C(gt_C), .D(D), .w_enb(and_1_out[9]), .rs1_enb(and_3_out[9]), .rs2_enb(and_2_out[9]), .rs1(rs1),
    .rs2(rs2));
  _32bit_Register _32bit_register_4 (
    .gt_C(gt_C), .D(D), .w_enb(and_1_out[16]), .rs1_enb(and_3_out[16]), .rs2_enb(and_2_out[16]), .rs1(rs1),
    .rs2(rs2));
  _32bit_Register _32bit_register_5 (
    .gt_C(gt_C), .D(D), .w_enb(and_1_out[24]), .rs1_enb(and_3_out_2[0]), .rs2_enb(and_2_out[24]), .rs1(rs1),
    .rs2(rs2));
  _32bit_Register _32bit_register_6 (
    .gt_C(gt_C), .D(D), .w_enb(and_1_out[2]), .rs1_enb(and_3_out[2]), .rs2_enb(and_2_out[2]), .rs1(rs1),
    .rs2(rs2));
  _32bit_Register _32bit_register_7 (
    .gt_C(gt_C), .D(D), .w_enb(and_1_out[17]), .rs1_enb(and_3_out[17]), .rs2_enb(and_2_out[17]), .rs1(rs1),
    .rs2(rs2));
  _32bit_Register _32bit_register_8 (
    .gt_C(gt_C), .D(D), .w_enb(and_1_out[10]), .rs1_enb(and_3_out[10]), .rs2_enb(and_2_out[10]), .rs1(rs1),
    .rs2(rs2));
  _32bit_Register _32bit_register_9 (
    .gt_C(gt_C), .D(D), .w_enb(and_1_out[25]), .rs1_enb(and_3_out_2[1]), .rs2_enb(and_2_out[25]), .rs1(rs1),
    .rs2(rs2));
  _32bit_Register _32bit_register_10 (
    .gt_C(gt_C), .D(D), .w_enb(and_1_out[3]), .rs1_enb(and_3_out[3]), .rs2_enb(and_2_out[3]), .rs1(rs1),
    .rs2(rs2));
  _32bit_Register _32bit_register_11 (
    .gt_C(gt_C), .D(D), .w_enb(and_1_out[11]), .rs1_enb(and_3_out[11]), .rs2_enb(and_2_out[11]), .rs1(rs1),
    .rs2(rs2));
  _32bit_Register _32bit_register_12 (
    .gt_C(gt_C), .D(D), .w_enb(and_1_out[18]), .rs1_enb(and_3_out[18]), .rs2_enb(and_2_out[18]), .rs1(rs1),
    .rs2(rs2));
  _32bit_Register _32bit_register_13 (
    .gt_C(gt_C), .D(D), .w_enb(and_1_out[26]), .rs1_enb(and_3_out_2[2]), .rs2_enb(and_2_out[26]), .rs1(rs1),
    .rs2(rs2));
  _32bit_Register _32bit_register_14 (
    .gt_C(gt_C), .D(D), .w_enb(and_1_out[4]), .rs1_enb(and_3_out[4]), .rs2_enb(and_2_out[4]), .rs1(rs1),
    .rs2(rs2));
  _32bit_Register _32bit_register_15 (
    .gt_C(gt_C), .D(D), .w_enb(and_1_out[19]), .rs1_enb(and_3_out[19]), .rs2_enb(and_2_out[19]), .rs1(rs1),
    .rs2(rs2));
  _32bit_Register _32bit_register_16 (
    .gt_C(gt_C), .D(D), .w_enb(and_1_out[12]), .rs1_enb(and_3_out[12]), .rs2_enb(and_2_out[12]), .rs1(rs1),
    .rs2(rs2));
  _32bit_Register _32bit_register_17 (
    .gt_C(gt_C), .D(D), .w_enb(and_1_out[27]), .rs1_enb(and_3_out_2[3]), .rs2_enb(and_2_out[27]), .rs1(rs1),
    .rs2(rs2));
  _32bit_Register _32bit_register_18 (
    .gt_C(gt_C), .D(D), .w_enb(and_1_out[5]), .rs1_enb(and_3_out[5]), .rs2_enb(and_2_out[5]), .rs1(rs1),
    .rs2(rs2));
  _32bit_Register _32bit_register_19 (
    .gt_C(gt_C), .D(D), .w_enb(and_1_out[13]), .rs1_enb(and_3_out[13]), .rs2_enb(and_2_out[13]), .rs1(rs1),
    .rs2(rs2));
  _32bit_Register _32bit_register_20 (
    .gt_C(gt_C), .D(D), .w_enb(and_1_out[20]), .rs1_enb(and_3_out[20]), .rs2_enb(and_2_out[20]), .rs1(rs1),
    .rs2(rs2));
  _32bit_Register _32bit_register_21 (
    .gt_C(gt_C), .D(D), .w_enb(and_1_out[28]), .rs1_enb(and_3_out_2[4]), .rs2_enb(and_2_out[28]), .rs1(rs1),
    .rs2(rs2));
  _32bit_Register _32bit_register_22 (
    .gt_C(gt_C), .D(D), .w_enb(and_1_out[6]), .rs1_enb(and_3_out[6]), .rs2_enb(and_2_out[6]), .rs1(rs1),
    .rs2(rs2));
  _32bit_Register _32bit_register_23 (
    .gt_C(gt_C), .D(D), .w_enb(and_1_out[21]), .rs1_enb(and_3_out[21]), .rs2_enb(and_2_out[21]), .rs1(rs1),
    .rs2(rs2));
  _32bit_Register _32bit_register_24 (
    .gt_C(gt_C), .D(D), .w_enb(and_1_out[14]), .rs1_enb(and_3_out[14]), .rs2_enb(and_2_out[14]), .rs1(rs1),
    .rs2(rs2));
  _32bit_Register _32bit_register_25 (
    .gt_C(gt_C), .D(D), .w_enb(and_1_out[29]), .rs1_enb(and_3_out_2[5]), .rs2_enb(and_2_out[29]), .rs1(rs1),
    .rs2(rs2));
  _32bit_Register _32bit_register_26 (
    .gt_C(gt_C), .D(D), .w_enb(and_1_out[7]), .rs1_enb(and_3_out[7]), .rs2_enb(and_2_out[7]), .rs1(rs1),
    .rs2(rs2));
  _32bit_Register _32bit_register_27 (
    .gt_C(gt_C), .D(D), .w_enb(and_1_out[15]), .rs1_enb(and_3_out[15]), .rs2_enb(and_2_out[15]), .rs1(rs1),
    .rs2(rs2));
  _32bit_Register _32bit_register_28 (
    .gt_C(gt_C), .D(D), .w_enb(and_1_out[22]), .rs1_enb(and_3_out[22]), .rs2_enb(and_2_out[22]), .rs1(rs1),
    .rs2(rs2));
  _32bit_Register _32bit_register_29 (
    .gt_C(gt_C), .D(D), .w_enb(and_1_out[30]), .rs1_enb(and_3_out_2[6]), .rs2_enb(and_2_out[30]), .rs1(rs1),
    .rs2(rs2));
  _32bit_Register _32bit_register_30 (
    .gt_C(gt_C), .D(D), .w_enb(and_1_out[23]), .rs1_enb(and_3_out[23]), .rs2_enb(and_2_out[23]), .rs1(rs1),
    .rs2(rs2));
  _32bit_Register _32bit_register_31 (
    .gt_C(gt_C), .D(D), .w_enb(and_1_out[31]), .rs1_enb(and_3_out_2[7]), .rs2_enb(and_2_out[31]), .rs1(rs1),
    .rs2(rs2));
endmodule
