// Digital circuit addr_word_sel.dig as structural Verilog
module addr_word_sel (
  input  addr,
  input  word,
  input  enb,
  output o
);

  wire or_1_out;

  or or_1 (or_1_out, addr, word);
  and and_1 (o, or_1_out, enb);
endmodule
