// Digital circuit pulse_generator.dig as structural Verilog
module pulse_generator (
  input  i,
  output o
);

  wire delay_1_out, not_1_out;

  not not_1 (not_1_out, i);
  Delay delay_1 (.in(not_1_out), .out(delay_1_out));
  and and_1 (o, i, delay_1_out);
endmodule
